# Fritzing sketch A3 - Cupola (saved by Fritzing 0.9.3b)
stripboards: 1

parts:
  Componente1 = Arduino Uno (Rev3)
  U1 = POT [package=pot_mammoth]
  M1 = Stepper Motor - Bipolar  # not connected

nets:
  N1: Componente1.A3, U1.A
  N2: Componente1.5V, U1.E
  N3: Componente1.GND, U1.S

notes:
  USB 5V
  DM860T
  60V 6A
  DIR -
  DIR +
  PUL -
  PUL +
  ENA -
  ENA +
  A +
  AC
  B -
  B +
  A -
