# Fritzing sketch AP-H - Antipanico e aiuti (saved by Fritzing 0.9.3b)
circuit board: 10cm x 6cm
stripboards: 1

parts:
  J14 = Camdenboss CTB0158-2 [part_number=CTB0158-2 package=THT]
  R1 = Resistor [tolerance=±5% resistance=220 package=THT]
  Teensy_3_5 = Teensy 3.1
  S1 = SWITCH-MOMENTARY-2 [package=tactile-switch-1101ne]

nets:
  N1: J14.pin1, R1.Pin_1, Teensy_3_5.A2/D16, S1.2
  N2: J14.pin2, Teensy_3_5.3V3, S1.1
  N3: R1.Pin_0, Teensy_3_5.AGND
  N4: Teensy_3_5.GND, Teensy_3_5.A0/D14, Teensy_3_5.A1/D15, Teensy_3_5.A3/D17, Teensy_3_5.A4/D18, Teensy_3_5.A5/D19, Teensy_3_5.A6/D20, Teensy_3_5.A7/D21, Teensy_3_5.A8/D22, Teensy_3_5.A9/D23

notes:
  USB 5V
