# Fritzing sketch G13 - Cyclette (saved by Fritzing 0.9.3b)
stripboards: 2

parts:
  J4 = Screw terminal - 2 pins [package=THT]
  J5 = Screw terminal - 2 pins [package=THT]
  J6 = Screw terminal - 2 pins [package=THT]
  Teensy_3_3 = Teensy 3.1
  J7 = Screw terminal - 2 pins [package=THT]
  J8 = Screw terminal - 2 pins [package=THT]
  J9 = Screw terminal - 2 pins [package=THT]
  J10 = Screw terminal - 2 pins [package=THT]
  J11 = Screw terminal - 2 pins [package=THT]
  J12 = screw terminal, 3 pins
  J13 = screw terminal, 3 pins
  J14 = screw terminal, 3 pins
  J15 = screw terminal, 3 pins
  J16 = screw terminal, 3 pins
  J17 = screw terminal, 3 pins
  Componente1 = FC-03 [chip_label=FC-03]
  Componente2 = FC-03 [chip_label=FC-03]
  Componente3 = FC-03 [chip_label=FC-03]
  Componente4 = FC-03 [chip_label=FC-03]
  Componente5 = FC-03 [chip_label=FC-03]
  Componente6 = FC-03 [chip_label=FC-03]

nets:
  GND: J4.pin1, J5.pin1, Teensy_3_3.AGND, J12.pin2, J13.pin2, J14.pin2, J15.pin2, J16.pin2, J17.pin2, Componente1.GND, Componente2.GND, Componente3.GND, Componente4.GND, Componente5.GND, Componente6.GND
  VCC: J4.pin2, J5.pin2, Teensy_3_3.3V3, J12.pin1, J13.pin3, J14.pin1, J15.pin3, J16.pin3, J17.pin3, Componente1.VCC, Componente2.VCC, Componente3.VCC, Componente4.VCC, Componente5.VCC, Componente6.VCC
  N1: J6.pin1, Teensy_3_3.A9/D23, J7.pin1, J12.pin3, Componente5.D0
  N2: J6.pin2, Teensy_3_3.A8/D22, J7.pin2, J14.pin3, Componente6.D0
  N3: Teensy_3_3.A4/D18, J9.pin2, J11.pin2, J16.pin1, Componente2.D0
  N4: Teensy_3_3.A5/D19, J9.pin1, J11.pin1, J13.pin1, Componente4.D0
  N5: Teensy_3_3.A6/D20, J8.pin2, J10.pin2, J17.pin1, Componente3.D0
  N6: Teensy_3_3.A7/D21, J8.pin1, J10.pin1, J15.pin1, Componente1.D0

notes:
  USB 5V

custom parts:
  FC-03: FC-03, LM393 IR Speed Sensor Encoder
