# Fritzing sketch G7 - Portafrutta (saved by Fritzing 0.9.3b)
stripboards: 1

parts:
  Teensy_3_4 = Teensy 3.1
  J6 = Screw terminal - 2 pins [package=THT]  # not connected
  J7 = Screw terminal - 2 pins [package=THT]
  Componente1 = HX711 Weighing Sensor Module
  Componente2 = HX711 Weighing Sensor Module
  Componente3 = HX711 Weighing Sensor Module
  J11 = Screw terminal - 2 pins [package=THT]
  J9 = Screw terminal - 2 pins [package=THT]
  J10 = Screw terminal - 2 pins [package=THT]
  J13 = screw terminal, 3 pins
  J8 = screw terminal, 3 pins

nets:
  GND: Teensy_3_4.GND, Componente1.GND, Componente2.GND, Componente3.GND, J13.pin1, J13.pin2, J13.pin3
  N1: Teensy_3_4.D2, Componente1.DT, J9.pin1
  N2: Teensy_3_4.D3, Componente1.SCK, J9.pin2
  N3: Teensy_3_4.D4, Componente2.DT, J10.pin1
  N4: Teensy_3_4.D5, Componente2.SCK, J10.pin2
  N5: Teensy_3_4.D6, Componente3.DT, J11.pin1
  N6: Teensy_3_4.D7, Componente3.SCK, J11.pin2
  VCC: Teensy_3_4.3V3, Componente1.VCC, Componente2.VCC, Componente3.VCC, J8.pin1, J8.pin2, J8.pin3
  N7: Teensy_3_4.VUSB, J7.pin1

notes:
  USB 5V
  Load Cell
