# Fritzing sketch H - Help_Cassa (saved by Fritzing 0.9.3b)
stripboards: 1

parts:
  J21 = Camdenboss CTB0158-2 [part_number=CTB0158-2 package=THT]
  R6 = Resistor [tolerance=±5% resistance=1M package=THT]
  Teensy_3_6 = Teensy 3.1
  C5 = Ceramic Capacitor [capacitance=100nF package="100 mil [THT, multilayer]"]
  C6 = Electrolytic Capacitor [capacitance=0.22mF package="100 mil [THT, electrolytic]"]
  J22 = Piezo Speaker
  U1 = DIODE-ZENER [package=diode-zener]
  R7 = Resistor [tolerance=±5% resistance=330 package=THT]

nets:
  N1: J21.pin1, R6.Pin_0, Teensy_3_6.AGND, J22.pin1, U1.A
  N2: J21.pin2, R6.Pin_1, J22.pin2, U1.C, R7.Pin_0
  N3: Teensy_3_6.A7/D21, R7.Pin_1
  N4: Teensy_3_6.Vin, C5.0, C6.-
  N5: C5.1, C6.+

notes:
  USB 5V
