# Fritzing sketch G1 - Scrigno (saved by Fritzing 0.9.3b)
perfboards: 2

parts:
  KY-1 = Keyes Relay [package=THT]
  R1 = Resistor [tolerance=±5% resistance=10k package=THT]
  R2 = Resistor [tolerance=±5% resistance=10k package=THT]
  R3 = Resistor [tolerance=±5% resistance=10k package=THT]
  R4 = Resistor [tolerance=±5% resistance=10k package=THT]
  R5 = Resistor [tolerance=±5% resistance=10k package=THT]
  R6 = Resistor [tolerance=±5% resistance=10k package=THT]
  R7 = Resistor [tolerance=±5% resistance=10k package=THT]
  R8 = Resistor [tolerance=±5% resistance=10k package=THT]
  R9 = Resistor [tolerance=±5% resistance=10k package=THT]
  R10 = Resistor [tolerance=±5% resistance=10k package=THT]
  Teensy2 = Teensy 3.6 (Basic)
  U3 = Header 12 [package=1x12_machine-pin-header_lock.004]
  U4 = Header 12 [package=1x12_machine-pin-header_lock.004]
  U5 = Header 12 [package=1x12_machine-pin-header_lock.004]
  U6 = Header 12 [package=1x12_machine-pin-header_lock.004]
  S11 = Pushbutton [package="[THT]"]
  LED11 = LED - 3mm [color="Red (633nm)" package="3 mm [THT]"]
  S12 = Pushbutton [package="[THT]"]
  LED12 = LED - 3mm [color="Red (633nm)" package="3 mm [THT]"]
  S13 = Pushbutton [package="[THT]"]
  LED13 = LED - 3mm [color="Red (633nm)" package="3 mm [THT]"]
  S14 = Pushbutton [package="[THT]"]
  LED14 = LED - 3mm [color="Red (633nm)" package="3 mm [THT]"]
  S15 = Pushbutton [package="[THT]"]
  S16 = Pushbutton [package="[THT]"]
  S17 = Pushbutton [package="[THT]"]
  S18 = Pushbutton [package="[THT]"]
  LED15 = LED - 3mm [color="Red (633nm)" package="3 mm [THT]"]
  LED16 = LED - 3mm [color="Red (633nm)" package="3 mm [THT]"]
  LED17 = LED - 3mm [color="Red (633nm)" package="3 mm [THT]"]
  LED18 = LED - 3mm [color="Red (633nm)" package="3 mm [THT]"]
  S19 = Pushbutton [package="[THT]"]
  LED19 = LED - 3mm [color="Red (633nm)" package="3 mm [THT]"]
  S20 = Pushbutton [package="[THT]"]
  LED20 = LED - 3mm [color="Red (633nm)" package="3 mm [THT]"]
  J1 = Camdenboss CTB0158-2 [part_number=CTB0158-2 package=THT]
  C1 = Ceramic Capacitor [capacitance=10nF package="100 mil [THT, multilayer]"]
  C2 = Ceramic Capacitor [capacitance=10nF package="100 mil [THT, multilayer]"]
  C3 = Ceramic Capacitor [capacitance=10nF package="100 mil [THT, multilayer]"]
  C4 = Ceramic Capacitor [capacitance=10nF package="100 mil [THT, multilayer]"]
  C5 = Ceramic Capacitor [capacitance=10nF package="100 mil [THT, multilayer]"]
  C6 = Ceramic Capacitor [capacitance=10nF package="100 mil [THT, multilayer]"]
  C7 = Ceramic Capacitor [capacitance=10nF package="100 mil [THT, multilayer]"]
  C8 = Ceramic Capacitor [capacitance=10nF package="100 mil [THT, multilayer]"]
  C9 = Ceramic Capacitor [capacitance=10nF package="100 mil [THT, multilayer]"]
  C10 = Ceramic Capacitor [capacitance=10nF package="100 mil [THT, multilayer]"]
  R11 = Resistor [tolerance=±5% resistance=1k package=THT]

nets:
  N1: KY-1.signal, Teensy2.D39, J1.pin1
  GND: KY-1.ground, Teensy2.GND, Teensy2.D25, Teensy2.D26, Teensy2.D27, Teensy2.D28, Teensy2.D29, Teensy2.D30, Teensy2.D31, Teensy2.D32, Teensy2.D33, Teensy2.D34, Teensy2.D35, Teensy2.D36, Teensy2.D37, Teensy2.D38, Teensy2.A21/DAC0, Teensy2.A22/DAC1, Teensy2.GND1, U5.12, J1.pin2, C1.1, C2.1, C3.1, C4.1, C5.1, C6.1, C7.1, C8.1, C9.1, C10.1
  N2: R1.Pin_0, Teensy2.D24, U5.2, C9.0
  N3: R1.Pin_1, R2.Pin_1, R3.Pin_1, R4.Pin_1, R5.Pin_1, R6.Pin_1, R7.Pin_1, R8.Pin_1, R9.Pin_1, R10.Pin_1, Teensy2.3V3, Teensy2.3V3_1
  N4: R2.Pin_0, Teensy2.D8, U5.3, C10.0
  N5: R3.Pin_0, Teensy2.D7, U5.4, C8.0
  N6: R4.Pin_0, Teensy2.D6, U5.5, C7.0
  N7: R5.Pin_0, Teensy2.D5, U5.6, C6.0
  N8: R6.Pin_0, Teensy2.D4, U5.7, C5.0
  N9: R7.Pin_0, Teensy2.D3, U5.8, C4.0
  N10: R8.Pin_0, Teensy2.D2, U5.9, C3.0
  N11: R9.Pin_0, Teensy2.D1, U5.10, C2.0
  N12: R10.Pin_0, Teensy2.D0, C1.0, R11.Pin_1
  N13: Teensy2.A0/D14, U4.11
  N14: Teensy2.A1/D15, U4.10
  N15: Teensy2.A2/D16, U4.9
  N16: Teensy2.A3/D17, U4.8
  N17: Teensy2.A4/D18, U4.7
  N18: Teensy2.A5/D19, U4.6
  N19: Teensy2.A6/D20, U4.5
  N20: Teensy2.A7/D21, U4.4
  N21: Teensy2.A8/D22, U4.3
  N22: Teensy2.A9/D23, U4.2
  N23: U3.2, S14.Pin_3, S14.Pin_4
  N24: U3.3, S13.Pin_3, S13.Pin_4
  N25: U3.4, S12.Pin_3, S12.Pin_4
  N26: U3.5, S11.Pin_3, S11.Pin_4
  N27: U3.6, S19.Pin_3, S19.Pin_4
  N28: U3.7, S20.Pin_3, S20.Pin_4
  N29: U3.8, S15.Pin_3, S15.Pin_4
  N30: U3.9, S16.Pin_3, S16.Pin_4
  N31: U3.10, S17.Pin_3, S17.Pin_4
  N32: U3.11, S18.Pin_3, S18.Pin_4
  N33: U5.11, R11.Pin_0
  N34: U6.2, LED14.anode
  N35: U6.3, LED13.anode
  N36: U6.4, LED12.anode
  N37: U6.5, LED11.anode
  N38: U6.6, LED19.anode
  N39: U6.7, LED20.anode
  N40: U6.8, LED15.anode
  N41: U6.9, LED18.anode
  N42: U6.10, LED16.anode
  N43: U6.11, LED17.anode
  N44: S11.Pin_1, S11.Pin_2, S12.Pin_1, S12.Pin_2, S13.Pin_1, S13.Pin_2, S14.Pin_1, S14.Pin_2, S15.Pin_1, S15.Pin_2, S16.Pin_1, S16.Pin_2, S17.Pin_1, S17.Pin_2, S18.Pin_1, S18.Pin_2, S19.Pin_1, S19.Pin_2, S20.Pin_1, S20.Pin_2
  N45: LED11.cathode, LED12.cathode, LED13.cathode, LED14.cathode, LED15.cathode, LED16.cathode, LED17.cathode, LED18.cathode, LED19.cathode, LED20.cathode

notes:
  elettrocalamita + diodo + snubber
  12V
  SSR
  su ogni pulsante

custom parts:
  Keyes Relay: The Keyes 5V relay module is suitable for SCM development, home appliance control. It uses a 5V~12V TIL control signal which can control DC / AC signal.
  Teensy 3.6 (Basic): The Teensy is a complete USB-based microcontoller development system, in a very small footprint, capable of implementing many types of projects. All programming is done via the USB port. No special programmer is needed, only a standard micro-USB cable and a PC or Macintosh with a USB port.
