# Fritzing sketch G10 - Bambole (saved by Fritzing 0.9.3b)
stripboards: 3

parts:
  J23 = Screw terminal - 2 pins [package=THT]
  R59 = Resistor [tolerance=±5% resistance=1k package=THT]
  D4 = Rectifier Diode [part_number=1N4001 package="300 mil [THT]"]
  Q5 = Basic FET N-Channel [package="TO220 [THT]"]
  J32 = screw terminal, 3 pins
  U2 = Luxeon LED [package=luxeon]
  Teensy_3_1 = Teensy 3.1  # not connected
  Componente2 = Adafruit MPR121
  R60 = Resistor [tolerance=±5% resistance=1k package=THT]
  D5 = Rectifier Diode [part_number=1N4001 package="300 mil [THT]"]
  Q6 = Basic FET N-Channel [package="TO220 [THT]"]
  J33 = screw terminal, 3 pins
  U3 = Luxeon LED [package=luxeon]
  J26 = screw terminal, 10 pins
  J34 = Screw terminal - 2 pins [package=THT]
  J35 = Screw terminal - 2 pins [package=THT]
  R61 = Resistor [tolerance=±5% resistance=1.5k package=THT]
  R62 = Resistor [tolerance=±5% resistance=1.5k package=THT]

nets:
  N1: J23.pin2, R60.Pin_1, J33.pin3
  N2: R59.Pin_0, Q5.gate
  N3: R59.Pin_1, J32.pin3, J26.pin2
  N4: D4.cathode, Q5.drain, J32.pin1, U2.C
  N5: D4.anode, Q5.source, J32.pin2, Componente2.GND, J26.pin1
  N6: Componente2.VIN, J34.pin2
  N7: Componente2.SDA, J26.pin9, J35.pin1, R62.Pin_1
  N8: Componente2.SCL, J26.pin8, J35.pin2, R61.Pin_1
  N9: R60.Pin_0, Q6.gate
  N10: D5.cathode, Q6.drain, J33.pin1, U3.C
  N11: D5.anode, Q6.source, J33.pin2
  N12: J26.pin3, R61.Pin_0, R62.Pin_0

notes:
  Stagnola
  x8
  5V 5A
  x2

custom parts:
  Adafruit MPR121: Add lots of touch sensors to your next microcontroller project with this easy-to-use 12-channel capacitive touch sensor breakout board, starring the MPR121. This chip can handle up to 12 individual touch pads. The MPR121 has support for only I2C, which can be implemented with nearly any microcontroller. You can select one of 4 addresses with the ADDR pin, for a total of 48 capacitive touch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
