# Fritzing sketch G10 - Xilofono (saved by Fritzing 0.9.3b)
stripboards: 1

parts:
  Teensy2 = Teensy 3.6 (Basic)
  S1 = Round Pushbutton
  LED1 = LED - 5mm [color="Red (633nm)" package="5 mm [THT]"]
  LED2 = LED - 5mm [color="Red (633nm)" package="5 mm [THT]"]
  S2 = Round Pushbutton
  S3 = Round Pushbutton
  S4 = Round Pushbutton
  S5 = Round Pushbutton
  S6 = Round Pushbutton
  S7 = Round Pushbutton
  S8 = Round Pushbutton
  S10 = SWITCH-MOMENTARY-2 [package=tactile-switch-1101ne]
  R10 = Resistor [tolerance=±5% resistance=10k package=THT]
  R11 = Resistor [tolerance=±5% resistance=10k package=THT]
  R13 = Resistor [tolerance=±5% resistance=10k package=THT]
  R14 = Resistor [tolerance=±5% resistance=10k package=THT]
  R15 = Resistor [tolerance=±5% resistance=10k package=THT]
  R16 = Resistor [tolerance=±5% resistance=10k package=THT]
  R18 = Resistor [tolerance=±5% resistance=10k package=THT]
  R20 = Resistor [tolerance=±5% resistance=10k package=THT]
  R22 = Resistor [tolerance=±5% resistance=10k package=THT]
  R23 = Resistor [tolerance=±5% resistance=10k package=THT]
  R24 = Resistor [tolerance=±5% resistance=10k package=THT]
  R17 = Resistor [tolerance=±5% resistance=10k package=THT]
  R21 = Resistor [tolerance=±5% resistance=10k package=THT]
  S11 = SWITCH-MOMENTARY-2 [package=tactile-switch-1101ne]
  S12 = SWITCH-MOMENTARY-2 [package=tactile-switch-1101ne]
  S13 = SWITCH-MOMENTARY-2 [package=tactile-switch-1101ne]
  S14 = SWITCH-MOMENTARY-2 [package=tactile-switch-1101ne]
  S15 = SWITCH-MOMENTARY-2 [package=tactile-switch-1101ne]
  J32 = Basic Servo
  JP2 = Header 2 [package=screwterminal-3.5mm-2_lock]
  J37 = Camdenboss CTB0158-2 [part_number=CTB0158-2 package=THT]
  J38 = Camdenboss CTB0158-2 [part_number=CTB0158-2 package=THT]
  J39 = Camdenboss CTB0158-2 [part_number=CTB0158-2 package=THT]
  IC2 = IC, DIP package, 4 pins [chip_label="SSR-25 DD"]
  IC3 = IC, DIP package, 4 pins [chip_label="SSR-25 DD"]
  IC4 = IC, DIP package, 4 pins [chip_label="SSR-25 DD"]
  IC5 = IC, DIP package, 4 pins [chip_label="SSR-25 DD"]
  IC6 = IC, DIP package, 4 pins [chip_label="SSR-25 DD"]
  IC7 = IC, DIP package, 4 pins [chip_label="SSR-25 DD"]
  J40 = Camdenboss CTB0158-2 [part_number=CTB0158-2 package=THT]
  J41 = Camdenboss CTB0158-2 [part_number=CTB0158-2 package=THT]
  J42 = Camdenboss CTB0158-2 [part_number=CTB0158-2 package=THT]
  J43 = Camdenboss CTB0158-2 [part_number=CTB0158-2 package=THT]
  J44 = Camdenboss CTB0158-2 [part_number=CTB0158-2 package=THT]
  J45 = Camdenboss CTB0158-2 [part_number=CTB0158-2 package=THT]
  J46 = Camdenboss CTB0158-2 [part_number=CTB0158-2 package=THT]
  J47 = Camdenboss CTB0158-2 [part_number=CTB0158-2 package=THT]
  J48 = Camdenboss CTB0158-2 [part_number=CTB0158-2 package=THT]
  J50 = Camdenboss CTB0158-2 [part_number=CTB0158-2 package=THT]
  J51 = Camdenboss CTB0158-2 [part_number=CTB0158-2 package=THT]
  J52 = Camdenboss CTB0158-2 [part_number=CTB0158-2 package=THT]
  J53 = Camdenboss CTB0158-2 [part_number=CTB0158-2 package=THT]
  J54 = Camdenboss CTB0158-2 [part_number=CTB0158-2 package=THT]
  J55 = Camdenboss CTB0158-2 [part_number=CTB0158-2 package=THT]
  R29 = Resistor [tolerance=±5% resistance=10k package=THT]
  J49 = Camdenboss CTB0158-3 [part_number=CTB0158-3 package=THT]

nets:
  GND: Teensy2.GND, Teensy2.GND1, S1.leg0, LED1.cathode, LED2.cathode, S2.leg0, S3.leg0, S4.leg0, S5.leg0, S6.leg0, S7.leg0, S8.leg0, S10.2, S11.2, S12.2, S13.2, S14.2, S15.2, J32.gnd, IC2.pin1, IC3.pin1, IC4.pin1, IC5.pin1, IC6.pin1, IC7.pin1, J49.pin1, J49.pin2, J49.pin3
  N1: Teensy2.D0, IC2.pin2, J48.pin1
  N2: Teensy2.D2, IC3.pin2, J48.pin2
  N3: Teensy2.D4, IC4.pin2, J46.pin1
  N4: Teensy2.D6, IC5.pin2, J46.pin2
  N5: Teensy2.D7, IC6.pin2, J47.pin2
  N6: Teensy2.D8, IC7.pin2, J47.pin1
  N7: Teensy2.A1/D15, S3.leg1, R23.Pin_1, J54.pin1
  N8: Teensy2.A2/D16, S7.leg1, R21.Pin_1, J50.pin1
  N9: Teensy2.A3/D17, S8.leg1, R17.Pin_1, J54.pin2
  N10: Teensy2.A4/D18, S6.leg1, R20.Pin_1, J50.pin2
  N11: Teensy2.A5/D19, S1.leg1, J52.pin1, R29.Pin_1
  N12: Teensy2.A6/D20, S5.leg1, R18.Pin_1, J53.pin1
  N13: Teensy2.A7/D21, LED1.anode, J52.pin2
  N14: Teensy2.A8/D22, S4.leg1, R24.Pin_1, J53.pin2
  N15: Teensy2.A9/D23, J32.pulse, J51.pin1
  N16: Teensy2.3V3, Teensy2.3V3_1, R10.Pin_1, R11.Pin_0, R13.Pin_0, R14.Pin_0, R15.Pin_0, R16.Pin_0, R18.Pin_0, R20.Pin_0, R22.Pin_0, R23.Pin_0, R24.Pin_0, R17.Pin_0, R21.Pin_0, R29.Pin_0
  VIN: Teensy2.Vin, J32.vcc, J51.pin2
  N17: Teensy2.D24, R11.Pin_1, S14.1, J37.pin2
  N18: Teensy2.D25, R10.Pin_0, S15.1, J37.pin1
  N19: Teensy2.D26, R13.Pin_1, S13.1, J38.pin1
  N20: Teensy2.D28, R16.Pin_1, S12.1, J38.pin2
  N21: Teensy2.D30, R14.Pin_1, S11.1, J39.pin1
  N22: Teensy2.D32, S10.1, R15.Pin_1, J39.pin2
  N23: Teensy2.D33, LED2.anode, J55.pin1
  N24: Teensy2.D35, S2.leg1, R22.Pin_1, J55.pin2
  N25: JP2.1, IC2.pin3
  N26: JP2.2, J40.pin2, J41.pin2, J42.pin2, J43.pin2, J44.pin2, J45.pin2
  N27: IC2.pin4, J40.pin1
  N28: IC3.pin4, J41.pin1
  N29: IC4.pin4, J42.pin1
  N30: IC5.pin3, IC6.pin3, IC7.pin3
  N31: IC5.pin4, J43.pin1
  N32: IC6.pin4, J45.pin1
  N33: IC7.pin4, J44.pin1

notes:
  Play
  Reset
  Trasformatore 12v 2A
  5V 5A
  Elettrovalvola
  10nF su tutti i pullup
  filtro 5v
  Tagliare pista del teensy

custom parts:
  Teensy 3.6 (Basic): The Teensy is a complete USB-based microcontoller development system, in a very small footprint, capable of implementing many types of projects. All programming is done via the USB port. No special programmer is needed, only a standard micro-USB cable and a PC or Macintosh with a USB port.
