# Fritzing sketch G11 - Tastierino (saved by Fritzing 0.9.3b)
stripboards: 1

parts:
  KEYPAD1 = Membrane Matrix Keypad
  Teensy_3_1 = Teensy 3.1  # not connected
  J1 = screw terminal, 7 pins
  R4 = Resistor [tolerance=±5% resistance=10k package=THT]
  C1 = Ceramic Capacitor [capacitance=100nF package="100 mil [THT, multilayer]"]
  C2 = Ceramic Capacitor [capacitance=100nF package="100 mil [THT, multilayer]"]
  C3 = Ceramic Capacitor [capacitance=100nF package="100 mil [THT, multilayer]"]
  C4 = Ceramic Capacitor [capacitance=100nF package="100 mil [THT, multilayer]"]
  R5 = Resistor [tolerance=±5% resistance=10k package=THT]
  R6 = Resistor [tolerance=±5% resistance=10k package=THT]
  R7 = Resistor [tolerance=±5% resistance=10k package=THT]
  C5 = Ceramic Capacitor [capacitance=100nF package="100 mil [THT, multilayer]"]
  C6 = Electrolytic Capacitor [capacitance=1µF package="100 mil [THT, electrolytic]"]

nets:
  N1: KEYPAD1.1, J1.pin1, R4.Pin_0, C1.1
  N2: KEYPAD1.7, J1.pin7
  N3: J1.pin2, C2.1, R5.Pin_0
  N4: J1.pin3, C3.1, R6.Pin_0
  N5: J1.pin4, C4.1, R7.Pin_0
  N6: R4.Pin_1, C1.0, C2.0, C3.0, C4.0, R5.Pin_1, R6.Pin_1, R7.Pin_1, C5.0, C5.1, C6.-, C6.+

notes:
  USB 5V
  capire quali pin sono pull-up

custom parts:
  Membrane Matrix Keypad: Membrane Matrix 3x4 Keypad
