# Fritzing sketch G2 - Freezer (saved by Fritzing 0.9.3b)
stripboards: 1

parts:
  S1 = Reed switch [package=THT]
  KY-1 = Keyes Relay [package=THT]
  C7 = Ceramic Capacitor [capacitance=10nF package="100 mil [THT, multilayer]"]
  C8 = Ceramic Capacitor [capacitance=100nF package="100 mil [THT, multilayer]"]
  C9 = Electrolytic Capacitor [capacitance=0.22mF package="100 mil [THT, electrolytic]"]
  D5 = Zener Diode [part_number=1N4732A breakdown_voltage=3.6V package="Melf DO-213 AB [SMD]"]
  D6 = Schottky Diode [part_number="SR104 RO" package="300 mil [THT]"]
  J22 = Camdenboss CTB0158-2 [part_number=CTB0158-2 package=THT]
  R9 = Resistor [tolerance=±5% resistance=10 package=THT]
  R10 = Resistor [tolerance=±5% resistance=1k package=THT]
  R11 = Resistor [tolerance=±5% resistance=10k package=THT]
  Teensy_3_7 = Teensy 3.1
  J23 = screw terminal, 3 pins

nets:
  N1: S1.pin_1, KY-1.ground, C7.0, D5.anode, J22.pin1, Teensy_3_7.AGND, J23.pin2
  N2: S1.pin_2, J22.pin2, R9.Pin_0
  N3: KY-1.signal, J23.pin3
  N4: KY-1.power, C8.0, C9.+, Teensy_3_7.Vin, J23.pin1
  N5: C7.1, R10.Pin_1, R11.Pin_1
  N6: C8.1, C9.-
  N7: D5.cathode, D6.anode, R9.Pin_1, R10.Pin_0
  N8: D6.cathode, R11.Pin_0, Teensy_3_7.3V3

notes:
  12V
  elettrocalamita + diodo + snubber
  USB 5V

custom parts:
  Keyes Relay: The Keyes 5V relay module is suitable for SCM development, home appliance control. It uses a 5V~12V TIL control signal which can control DC / AC signal.
