# Fritzing sketch G3 - Imbuto (saved by Fritzing 0.9.3b)
stripboards: 1

parts:
  S2 = Tactile Switch Buttons - 12mm Square [package=tactile-pth-12mm]
  J6 = Screw terminal - 2 pins [package=THT]
  R3 = Resistor [tolerance=±5% resistance=10k package=THT]
  Teensy_3_2 = Teensy 3.1  # not connected

nets:
  N1: S2.1, S2.3, J6.pin1
  N2: S2.4, J6.pin2, R3.Pin_1

notes:
  USB 5V

custom parts:
  Tactile Switch Buttons - 12mm Square: Medium-sized clicky momentary switches are standard input "buttons" on electronic projects. These work best in a PCB but can be used on a solderless breadboard as shown in this tutorial. The pins are normally open (disconnected) and when the button is pressed they are momentarily closed. They come in a pack of 10, they're pretty handy so you'll want to keep them around. You can find an EAGLE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
