# Fritzing sketch G5 - Cestino (saved by Fritzing 0.9.3b)
stripboards: 3

parts:
  J4 = Screw terminal - 2 pins [package=THT]
  J5 = Screw terminal - 2 pins [package=THT]
  J6 = Screw terminal - 2 pins [package=THT]
  Teensy_3_3 = Teensy 3.1
  M1 = fc-51 [package=THT]
  J7 = Screw terminal - 2 pins [package=THT]
  J8 = Screw terminal - 2 pins [package=THT]
  J9 = Screw terminal - 2 pins [package=THT]
  M2 = fc-51 [package=THT]
  M3 = fc-51 [package=THT]
  M4 = fc-51 [package=THT]
  M5 = fc-51 [package=THT]
  M6 = fc-51 [package=THT]
  J10 = Screw terminal - 2 pins [package=THT]
  J11 = Screw terminal - 2 pins [package=THT]
  J12 = screw terminal, 3 pins
  J13 = screw terminal, 3 pins
  J14 = screw terminal, 3 pins
  J15 = screw terminal, 3 pins
  J16 = screw terminal, 3 pins
  J17 = screw terminal, 3 pins
  C1 = Ceramic Capacitor [capacitance=100nF package="100 mil [THT, multilayer]"]
  C2 = Ceramic Capacitor [capacitance=100nF package="100 mil [THT, multilayer]"]
  J18 = Screw terminal - 2 pins [package=THT]
  J19 = screw terminal, 3 pins
  J20 = screw terminal, 3 pins
  J21 = screw terminal, 3 pins
  J22 = screw terminal, 3 pins
  J23 = screw terminal, 3 pins
  J24 = screw terminal, 3 pins
  J25 = Screw terminal - 2 pins [package=THT]
  J26 = Screw terminal - 2 pins [package=THT]
  J27 = Screw terminal - 2 pins [package=THT]
  IC1 = '4050 Hex Buffer

nets:
  N1: J4.pin1, J5.pin1, Teensy_3_3.AGND, M1.pin2, M2.pin2, M3.pin2, M4.pin2, M5.pin2, M6.pin2, J12.pin2, J13.pin2, J14.pin2, J15.pin2, J16.pin2, J17.pin2, C1.0
  N2: J4.pin2, J5.pin2, Teensy_3_3.Vin, M1.pin3, M2.pin3, M3.pin3, M4.pin3, M5.pin3, M6.pin3, J12.pin1, J13.pin3, J14.pin1, J15.pin3, J16.pin3, J17.pin3, C1.1
  N3: J6.pin1, Teensy_3_3.A9/D23, M1.pin1, J7.pin1, J12.pin3
  N4: J6.pin2, Teensy_3_3.A8/D22, J7.pin2, M2.pin1, J14.pin3
  N5: Teensy_3_3.GND, Teensy_3_3.D0, Teensy_3_3.D1, Teensy_3_3.D2, Teensy_3_3.D3, Teensy_3_3.D4, Teensy_3_3.D5, Teensy_3_3.D6, Teensy_3_3.D7, Teensy_3_3.D8, Teensy_3_3.A0/D14, Teensy_3_3.A1/D15, Teensy_3_3.A2/D16, Teensy_3_3.A3/D17
  N6: Teensy_3_3.A4/D18, J9.pin2, M4.pin1, J11.pin2, J16.pin1
  N7: Teensy_3_3.A5/D19, J9.pin1, M6.pin1, J11.pin1, J13.pin1
  N8: Teensy_3_3.A6/D20, J8.pin2, M5.pin1, J10.pin2, J17.pin1
  N9: Teensy_3_3.A7/D21, J8.pin1, M3.pin1, J10.pin1, J15.pin1
  N10: C2.0, J18.pin1, J20.pin2, J21.pin2, J22.pin2, J24.pin2
  N11: C2.1, J18.pin2, J22.pin1, J24.pin1, IC1.VCC
  N12: J19.pin1, IC1.E
  N13: J19.pin2, J23.pin2, IC1.VSS
  N14: J19.pin3, J20.pin3, J21.pin3, J23.pin3
  N15: J20.pin1, IC1.D
  N16: J21.pin1, IC1.B
  N17: J22.pin3, IC1.F
  N18: J23.pin1, IC1.C
  N19: J24.pin3, IC1.A
  N20: J25.pin1, IC1.I
  N21: J25.pin2, IC1.J
  N22: J26.pin1, IC1.H
  N23: J26.pin2, IC1.K
  N24: J27.pin1, IC1.G
  N25: J27.pin2, IC1.L

notes:
  USB 5V
  se da problemi mettere 74LS541 (trigger di schmitt) all'uscita degli IR per trasformare il segnale da analogico a digitale
  (G1 e G2 a massa)
