# Fritzing sketch G6 - Carillon (saved by Fritzing 0.9.3b)
stripboards: 1

parts:
  S2 = Tactile Switch Buttons - 12mm Square [package=tactile-pth-12mm]
  S3 = Tactile Switch Buttons - 12mm Square [package=tactile-pth-12mm]
  S4 = Tactile Switch Buttons - 12mm Square [package=tactile-pth-12mm]
  S5 = Tactile Switch Buttons - 12mm Square [package=tactile-pth-12mm]
  S6 = Tactile Switch Buttons - 12mm Square [package=tactile-pth-12mm]
  S7 = Tactile Switch Buttons - 12mm Square [package=tactile-pth-12mm]
  S8 = Tactile Switch Buttons - 12mm Square [package=tactile-pth-12mm]
  S9 = Tactile Switch Buttons - 12mm Square [package=tactile-pth-12mm]
  S10 = Tactile Switch Buttons - 12mm Square [package=tactile-pth-12mm]
  R12 = Resistor [tolerance=±5% resistance=10k package=THT]
  R13 = Resistor [tolerance=±5% resistance=10k package=THT]
  R14 = Resistor [tolerance=±5% resistance=10k package=THT]
  R15 = Resistor [tolerance=±5% resistance=10k package=THT]
  R17 = Resistor [tolerance=±5% resistance=10k package=THT]
  R18 = Resistor [tolerance=±5% resistance=10k package=THT]
  R19 = Resistor [tolerance=±5% resistance=10k package=THT]
  R20 = Resistor [tolerance=±5% resistance=10k package=THT]
  J14 = Camdenboss CTB0158-2 [part_number=CTB0158-2 package=THT]
  J15 = Camdenboss CTB0158-2 [part_number=CTB0158-2 package=THT]
  J16 = Camdenboss CTB0158-2 [part_number=CTB0158-2 package=THT]
  J17 = Camdenboss CTB0158-2 [part_number=CTB0158-2 package=THT]
  R16 = Resistor [tolerance=±5% resistance=10k package=THT]
  Teensy_3_3 = Teensy 3.1
  J18 = Camdenboss CTB0158-2 [part_number=CTB0158-2 package=THT]
  J19 = screw terminal, 3 pins
  C1 = Ceramic Capacitor [capacitance=10nF package="100 mil [THT, multilayer]"]
  C2 = Ceramic Capacitor [capacitance=10nF package="100 mil [THT, multilayer]"]
  C3 = Ceramic Capacitor [capacitance=10nF package="100 mil [THT, multilayer]"]
  C5 = Ceramic Capacitor [capacitance=100nF package="100 mil [THT, multilayer]"]
  C7 = Ceramic Capacitor [capacitance=100nF package="100 mil [THT, multilayer]"]
  C9 = Ceramic Capacitor [capacitance=100nF package="100 mil [THT, multilayer]"]
  C11 = Ceramic Capacitor [capacitance=100nF package="100 mil [THT, multilayer]"]
  C12 = Ceramic Capacitor [capacitance=100nF package="100 mil [THT, multilayer]"]
  C13 = Ceramic Capacitor [capacitance=100nF package="100 mil [THT, multilayer]"]
  C14 = Ceramic Capacitor [capacitance=100nF package="100 mil [THT, multilayer]"]
  C15 = Electrolytic Capacitor [capacitance=1µF package="100 mil [THT, electrolytic]"]

nets:
  N1: S2.1, S2.3, S3.1, S3.3, S4.1, S4.3, S5.1, S5.3, S6.1, S6.3, S7.3, S8.3, S9.3, S10.3, Teensy_3_3.AGND, J18.pin2, C1.0, C2.0, C3.0, C5.0, C7.0, C9.0, C11.0, C12.0, C13.0
  N2: S2.4, R17.Pin_1, J15.pin2, Teensy_3_3.A8/D22, C2.1
  N3: S3.2, S3.4, R20.Pin_1, J16.pin1, Teensy_3_3.A1/D15, C13.1
  N4: S4.2, S4.4, R12.Pin_1, J16.pin2, Teensy_3_3.A3/D17, C11.1
  N5: S5.4, R15.Pin_1, J14.pin1, Teensy_3_3.A2/D16, C12.1
  N6: S6.2, S6.4, R13.Pin_1, J14.pin2, Teensy_3_3.A4/D18, C9.1
  N7: S7.2, S7.4, J15.pin1, R16.Pin_1, Teensy_3_3.A6/D20, C5.1
  N8: S8.4, R14.Pin_1, J17.pin1, Teensy_3_3.A5/D19, C7.1
  N9: S9.2, S9.4, R19.Pin_1, J17.pin2, Teensy_3_3.A7/D21, C3.1
  N10: S10.4, R18.Pin_1, Teensy_3_3.A9/D23, J18.pin1, C1.1
  N11: R12.Pin_0, R13.Pin_0, R14.Pin_0, R15.Pin_0, R17.Pin_0, R18.Pin_0, R19.Pin_0, R20.Pin_0, R16.Pin_0, Teensy_3_3.3V3
  N12: Teensy_3_3.Vin, J19.pin2
  N13: C14.0, C15.-
  N14: C14.1, C15.+

notes:
  Buzzer
  USB 5V
  condensatori sui pull-up

custom parts:
  Tactile Switch Buttons - 12mm Square: Medium-sized clicky momentary switches are standard input "buttons" on electronic projects. These work best in a PCB but can be used on a solderless breadboard as shown in this tutorial. The pins are normally open (disconnected) and when the button is pressed they are momentarily closed. They come in a pack of 10, they're pretty handy so you'll want to keep them around. You can find an EAGLE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
