# Fritzing sketch G7 - Portafrutta (saved by Fritzing 0.9.3b)
stripboards: 1

parts:
  Teensy_3_4 = Teensy 3.1
  J6 = Screw terminal - 2 pins [package=THT]  # not connected
  J7 = Screw terminal - 2 pins [package=THT]
  J11 = Screw terminal - 2 pins [package=THT]
  J9 = Screw terminal - 2 pins [package=THT]
  J10 = Screw terminal - 2 pins [package=THT]
  J13 = screw terminal, 3 pins
  J8 = screw terminal, 3 pins
  Componente3 = HX711 Weighing Sensor Module
  Componente1 = HX711 Weighing Sensor Module
  Componente2 = HX711 Weighing Sensor Module

nets:
  GND: Teensy_3_4.GND, J13.pin1, J13.pin2, J13.pin3, Componente3.GND, Componente1.GND, Componente2.GND
  N1: Teensy_3_4.D2, J9.pin1, Componente1.DO/RX
  N2: Teensy_3_4.D3, J9.pin2, Componente1.CK/TX
  N3: Teensy_3_4.D4, J10.pin1, Componente2.DO/RX
  N4: Teensy_3_4.D5, J10.pin2, Componente2.CK/TX
  N5: Teensy_3_4.D6, J11.pin1, Componente3.DO/RX
  N6: Teensy_3_4.D7, J11.pin2, Componente3.CK/TX
  VCC: Teensy_3_4.3V3, J8.pin1, J8.pin2, J8.pin3, Componente3.VCC, Componente1.VCC, Componente2.VCC
  N7: Teensy_3_4.VUSB, J7.pin1

notes:
  USB 5V
  Load Cell
