# Fritzing sketch G8 - Essenze (saved by Fritzing 0.9.3b)
stripboards: 1

parts:
  Componente3 = RFID-RC522-v2
  Teensy_3_4 = Teensy 3.1
  J10 = Screw terminal - 2 pins [package=THT]
  Componente4 = RFID-RC522-v2
  J11 = Screw terminal - 2 pins [package=THT]
  J12 = Screw terminal - 2 pins [package=THT]
  J13 = Screw terminal - 2 pins [package=THT]
  J14 = screw terminal, 8 pins
  J16 = screw terminal, 8 pins
  J19 = Screw terminal - 2 pins [package=THT]
  J22 = Screw terminal - 2 pins [package=THT]
  J23 = Screw terminal - 2 pins [package=THT]
  LED1 = LEDs [package=led10mm]
  R1 = Resistor [tolerance=±5% resistance=100 package=THT]
  C1 = Ceramic Capacitor [capacitance=100nF package="100 mil [THT, multilayer]"]
  C2 = Electrolytic Capacitor [capacitance=1µF package="100 mil [THT, electrolytic]"]

nets:
  N1: Componente3.SDA, Teensy_3_4.A1/D15, J13.pin1
  N2: Componente3.SCK, Teensy_3_4.D13, Componente4.SCK, J12.pin1, J22.pin1
  N3: Componente3.MOSI, Teensy_3_4.D11, Componente4.MOSI, J11.pin1, J23.pin1
  N4: Componente3.MISO, Teensy_3_4.D12, Componente4.MISO, J11.pin2, J23.pin2
  GND: Componente3.GND, Teensy_3_4.AGND, J10.pin2, Componente4.GND, J19.pin2, C1.1, C2.-
  N5: Componente3.RST, Teensy_3_4.A2/D16, Componente4.RST, J13.pin2, J22.pin2
  3.3V: Componente3.3.3V, Teensy_3_4.3V3, J10.pin1, Componente4.3.3V, J19.pin1
  N6: Teensy_3_4.GND, J16.pin1, J16.pin2, J16.pin3, J16.pin4, J16.pin5, J16.pin6, J16.pin7, J16.pin8, LED1.A
  N7: Teensy_3_4.D0, J14.pin1, R1.Pin_0
  N8: Teensy_3_4.D1, J14.pin2
  N9: Teensy_3_4.D2, J14.pin3
  N10: Teensy_3_4.D3, J14.pin4
  N11: Teensy_3_4.D4, J14.pin5
  N12: Teensy_3_4.D5, J14.pin6
  N13: Teensy_3_4.D6, J14.pin7
  N14: Teensy_3_4.D7, J14.pin8
  N15: Teensy_3_4.A0/D14, Componente4.SDA, J12.pin2
  N16: Teensy_3_4.Vin, C1.0, C2.+

notes:
  5V USB
  x 8
  cavo schermato

custom parts:
  RFID-RC522-v2: A simple China made RFID-RC522 Reader; do check the pin labels, as this is a MFRC522 based clone.
