# Fritzing sketch G1 - Consolle (saved by Fritzing 0.9.3b)
stripboards: 1

parts:
  S9 = Round Pushbutton
  S10 = Round Pushbutton
  S11 = Round Pushbutton
  S12 = Round Pushbutton
  KY-1 = Keyes Relay [package=THT]
  Water_Level_Sensor1 = Water Level Sensor
  D2F1 = D2F-FL Omron Snap Action Limit Switch with Level
  R1 = Resistor [tolerance=±5% resistance=10k package=THT]
  KY-2 = Keyes Relay [package=THT]
  D2F2 = D2F-FL Omron Snap Action Limit Switch with Level
  KY-3 = Keyes Relay [package=THT]
  R2 = Resistor [tolerance=±5% resistance=10k package=THT]
  R3 = Resistor [tolerance=±5% resistance=10k package=THT]
  Teensy_3_2 = Teensy 3.1
  J5 = Camdenboss CTB0158-2 [part_number=CTB0158-2 package=THT]
  J6 = Camdenboss CTB0158-3 [part_number=CTB0158-3 package=THT]
  J7 = Camdenboss CTB0158-2 [part_number=CTB0158-2 package=THT]
  J8 = Camdenboss CTB0158-2 [part_number=CTB0158-2 package=THT]
  J9 = Camdenboss CTB0158-2 [part_number=CTB0158-2 package=THT]
  J10 = Camdenboss CTB0158-2 [part_number=CTB0158-2 package=THT]
  J11 = Camdenboss CTB0158-2 [part_number=CTB0158-2 package=THT]

nets:
  N1: S9.leg0, S10.leg0, S11.leg0, S12.leg0, Water_Level_Sensor1.GND, D2F1.NO, D2F2.NO, Teensy_3_2.AGND, J5.pin2, J6.pin2, J7.pin2, J8.pin2
  N2: S9.leg1, S10.leg1, S11.leg1, S12.leg1, R1.Pin_1, Teensy_3_2.A7/D21, J5.pin1
  N3: KY-1.signal, KY-2.signal, KY-3.signal, Teensy_3_2.D2, Teensy_3_2.D4, Teensy_3_2.D6, J10.pin1, J10.pin2, J11.pin1, J11.pin2
  N4: KY-1.power, KY-2.power, KY-3.power, J9.pin1
  N5: KY-1.ground, KY-2.ground, KY-3.ground, Teensy_3_2.GND, J9.pin2
  N6: Water_Level_Sensor1.SIG, Teensy_3_2.A9/D23, J6.pin3
  VCC: Water_Level_Sensor1.VCC, Teensy_3_2.Vin, J6.pin1
  N7: D2F1.COM, R3.Pin_1, Teensy_3_2.A3/D17, J7.pin1
  N8: R1.Pin_0, R2.Pin_0, R3.Pin_0, Teensy_3_2.3V3
  N9: D2F2.COM, R2.Pin_1, Teensy_3_2.A2/D16, J8.pin1

notes:
  macchina fumo
  (collegare su CTL)
  sportello ingranaggi
  (collegare su CLT)
  fiaccola
  Ingranaggio
  motore ingranaggi
  - Pulsanti tutti pullup completi di diodi
  - Servo ok
  - Acqua collegato con cavo schermato
  - Fumo eventualmente relay 15A
  - sportello elettropistoni
  - motore mosfet con pulldown 10k
  MASSE DEGLI ALIMENTATORI TUTTE IN COMUNE, ANCHE COL DISPOSITIVO

custom parts:
  Keyes Relay: The Keyes 5V relay module is suitable for SCM development, home appliance control. It uses a 5V~12V TIL control signal which can control DC / AC signal.
  Water Level Sensor: A water level sensor. This sensor operates at 3V to 5V. The Sig (signal) pin outputs an analogue signal that is in proportion to the amount of water in contact with the sensor.
  D2F-FL Omron Snap Action Limit Switch with Level: Snap action switch with stainless steel lever.
