# Fritzing sketch G10 - Uova (saved by Fritzing 0.9.3b)
stripboards: 1

parts:
  Teensy_3_2 = Teensy 3.1
  Componente3 = Adafruit MPR121
  J37 = Screw terminal - 2 pins [package=THT]
  J38 = Screw terminal - 2 pins [package=THT]
  U5 = Luxeon LED [package=luxeon]
  J36 = screw terminal, 8 pins
  C9 = Ceramic Capacitor [capacitance=100nF package="100 mil [THT, multilayer]"]
  C10 = Electrolytic Capacitor [capacitance=1µF package="100 mil [THT, electrolytic]"]
  KY-1 = Keyes Relay [package=THT]
  J39 = Camdenboss CTB0158-2 [part_number=CTB0158-2 package=THT]

nets:
  N1: Teensy_3_2.GND, C9.0, C10.-, KY-1.ground, J39.pin2
  N2: Teensy_3_2.D1, J36.pin1, KY-1.signal
  N3: Teensy_3_2.D2, J36.pin2
  N4: Teensy_3_2.D3, J36.pin3
  N5: Teensy_3_2.D4, Teensy_3_2.D5, J36.pin4
  N6: Teensy_3_2.A4/D18, Componente3.SDA, J37.pin1
  N7: Teensy_3_2.A5/D19, Componente3.SCL, J37.pin2
  3V3: Teensy_3_2.3V3, Componente3.3.3V, J38.pin2
  N8: Teensy_3_2.AGND, Componente3.GND, J38.pin1
  N9: Teensy_3_2.Vin, C9.1, C10.+, KY-1.power, J39.pin1
  N10: U5.A, KY-1.NO

notes:
  12V 5A
  x6
  Stagnola
  relay al posto del mosfet

custom parts:
  Adafruit MPR121: Add lots of touch sensors to your next microcontroller project with this easy-to-use 12-channel capacitive touch sensor breakout board, starring the MPR121. This chip can handle up to 12 individual touch pads. The MPR121 has support for only I2C, which can be implemented with nearly any microcontroller. You can select one of 4 addresses with the ADDR pin, for a total of 48 capacitive touch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
  Keyes Relay: The Keyes 5V relay module is suitable for SCM development, home appliance control. It uses a 5V~12V TIL control signal which can control DC / AC signal.
