# Fritzing sketch G11 - Braciere (saved by Fritzing 0.9.3b)
stripboards: 1

parts:
  Teensy_3_2 = Teensy 3.1  # not connected
  D2F5 = D2F-FL Omron Snap Action Limit Switch with Level
  J6 = Screw terminal - 2 pins [package=THT]
  J7 = screw terminal, 3 pins
  J8 = Screw terminal - 2 pins [package=THT]
  R6 = Resistor [tolerance=±5% resistance=10k package=THT]
  KY-1 = Keyes Relay [package=THT]
  R7 = Resistor [tolerance=±5% resistance=10k package=THT]
  J5 = Screw terminal - 2 pins [package=THT]
  D2F6 = D2F-FL Omron Snap Action Limit Switch with Level

nets:
  N1: D2F5.COM, J7.pin1, J7.pin2, J7.pin3, KY-1.ground, D2F6.COM
  N2: D2F5.NO, R6.Pin_1, J5.pin2
  N3: J6.pin1, KY-1.signal
  N4: J8.pin1, J8.pin2, KY-1.power
  N5: R6.Pin_0, R7.Pin_0
  N6: R7.Pin_1, J5.pin1, D2F6.NO

notes:
  USB 5V
  12V
  elettrocalamita + diodo + snubber

custom parts:
  D2F-FL Omron Snap Action Limit Switch with Level: Snap action switch with stainless steel lever.
  Keyes Relay: The Keyes 5V relay module is suitable for SCM development, home appliance control. It uses a 5V~12V TIL control signal which can control DC / AC signal.
