# Fritzing sketch G11 - Pupazzo (saved by Fritzing 0.9.3b)
stripboards: 1

parts:
  Componente6 = HX711 Weighing Sensor Module
  J18 = Screw terminal - 2 pins [package=THT]
  J19 = screw terminal, 3 pins
  J20 = screw terminal, 3 pins
  Teensy_3_1 = Teensy 3.1  # not connected

nets:
  N1: Componente6.VCC, J20.pin1, J20.pin2, J20.pin3
  N2: Componente6.GND, J19.pin1, J19.pin2, J19.pin3
  N3: Componente6.DO/RX, J18.pin1
  N4: Componente6.CK/TX, J18.pin2

notes:
  USB 5V
  Load Cell
