# Fritzing sketch G11 - Uccelli (saved by Fritzing 0.9.3b)
stripboards: 1

parts:
  R2 = Resistor [tolerance=±5% resistance=10k package=THT]
  Teensy_LC = Teensy 3.1
  D2F1 = D2F-FL Omron Snap Action Limit Switch with Level
  D2F2 = D2F-FL Omron Snap Action Limit Switch with Level
  D2F3 = D2F-FL Omron Snap Action Limit Switch with Level
  R3 = Resistor [tolerance=±5% resistance=10k package=THT]
  R4 = Resistor [tolerance=±5% resistance=10k package=THT]
  C7 = Ceramic Capacitor [capacitance=100nF package="100 mil [THT, multilayer]"]
  C8 = Electrolytic Capacitor [capacitance=1µF package="100 mil [THT, electrolytic]"]
  J1 = screw terminal, 4 pins

nets:
  N1: R2.Pin_0, Teensy_LC.3V3, R3.Pin_0, R4.Pin_0
  N2: R2.Pin_1, Teensy_LC.A6/D20, D2F1.NO, J1.pin3
  N3: Teensy_LC.GND, C7.0, C8.-
  N4: Teensy_LC.A4/D18, D2F3.NO, R4.Pin_1, J1.pin1
  N5: Teensy_LC.A5/D19, D2F2.NO, R3.Pin_1, J1.pin2
  N6: Teensy_LC.Vin, C7.1, C8.+
  N7: D2F1.COM, D2F2.COM, D2F3.COM, J1.pin4

notes:
  USB 5V

custom parts:
  D2F-FL Omron Snap Action Limit Switch with Level: Snap action switch with stainless steel lever.
