# Fritzing sketch G13 - Forno (saved by Fritzing 0.9.3b)
stripboards: 1

parts:
  Teensy_3_1 = Teensy 3.1  # not connected
  U1 = POT_SWITCH [package=pot_pth_switch]
  U2 = POT_SWITCH [package=pot_pth_switch]
  KY-2 = Keyes Relay [package=THT]
  J4 = screw terminal, 3 pins
  J7 = screw terminal, 3 pins
  J30 = screw terminal, 8 pins
  J31 = screw terminal, 8 pins
  Componente6 = RFID-RC522-v2
  Componente7 = RFID-RC522-v2
  D2F1 = D2F-FL Omron Snap Action Limit Switch with Level
  R1 = Resistor [tolerance=±5% resistance=10k package=THT]
  J32 = Camdenboss CTB0158-2 [part_number=CTB0158-2 package=THT]
  J33 = Basic Servo
  J34 = Camdenboss CTB0158-2 [part_number=CTB0158-2 package=THT]
  J35 = Camdenboss CTB0158-2 [part_number=CTB0158-2 package=THT]
  J36 = Camdenboss CTB0158-2 [part_number=CTB0158-2 package=THT]

nets:
  3.3V: U1.G$1_A, U2.G$1_A, J30.pin1, J31.pin1, Componente6.3.3V, Componente7.3.3V, J35.pin1
  N1: U1.G$2_1, J30.pin4, J36.pin2
  GND: U1.G$2_2, U2.G$2_2, J30.pin3, J31.pin3, Componente6.GND, Componente7.GND, J35.pin2
  N2: U2.G$2_1, J31.pin4, J36.pin1
  N3: KY-2.signal, J7.pin3
  N4: KY-2.power, J4.pin1, J7.pin2, R1.Pin_0, J33.vcc, J34.pin2
  N5: KY-2.ground, J4.pin2, J7.pin1, D2F1.NO, J32.pin2, J33.gnd, J34.pin1
  N6: J4.pin3, J33.pulse
  N7: J30.pin2, J31.pin2, Componente6.RST, Componente7.RST
  N8: J30.pin5, J31.pin5, Componente6.MISO, Componente7.MISO
  N9: J30.pin6, J31.pin6, Componente6.MOSI, Componente7.MOSI
  N10: J30.pin7, J31.pin7, Componente6.SCK, Componente7.SCK
  N11: J30.pin8, Componente6.SDA
  N12: J31.pin8, Componente7.SDA
  N13: D2F1.COM, R1.Pin_1, J32.pin1

notes:
  5V 5A
  12V 3A
  elettrocalamita + diodo + snubber

custom parts:
  Keyes Relay: The Keyes 5V relay module is suitable for SCM development, home appliance control. It uses a 5V~12V TIL control signal which can control DC / AC signal.
  RFID-RC522-v2: A simple China made RFID-RC522 Reader; do check the pin labels, as this is a MFRC522 based clone.
  D2F-FL Omron Snap Action Limit Switch with Level: Snap action switch with stainless steel lever.
