# Fritzing sketch G13 - ManiglieBis (saved by Fritzing 0.9.3b)
stripboards: 1

parts:
  R2 = Resistor [tolerance=±5% resistance=10k package=THT]
  Teensy_LC = Teensy 3.1
  D2F1 = D2F-FL Omron Snap Action Limit Switch with Level
  KY-2 = Keyes Relay [package=THT]
  D2F2 = D2F-FL Omron Snap Action Limit Switch with Level
  D2F3 = D2F-FL Omron Snap Action Limit Switch with Level
  D2F4 = D2F-FL Omron Snap Action Limit Switch with Level
  R3 = Resistor [tolerance=±5% resistance=10k package=THT]
  R4 = Resistor [tolerance=±5% resistance=10k package=THT]
  R5 = Resistor [tolerance=±5% resistance=10k package=THT]
  LED3 = LEDs [package=led10mm]
  C7 = Ceramic Capacitor [capacitance=100nF package="100 mil [THT, multilayer]"]
  C8 = Electrolytic Capacitor [capacitance=1µF package="100 mil [THT, electrolytic]"]
  J3 = screw terminal, 3 pins
  J1 = screw terminal, 5 pins

nets:
  N1: R2.Pin_0, Teensy_LC.3V3, R3.Pin_0, R4.Pin_0, R5.Pin_0
  N2: R2.Pin_1, Teensy_LC.A6/D20, D2F1.NO, J1.pin4
  N3: Teensy_LC.GND, KY-2.power, C7.0, C8.-, J3.pin2
  N4: Teensy_LC.D5, KY-2.signal, J3.pin3
  N5: Teensy_LC.A3/D17, D2F4.NO, R5.Pin_1, J1.pin1
  N6: Teensy_LC.A4/D18, D2F3.NO, R4.Pin_1, J1.pin2
  N7: Teensy_LC.A5/D19, D2F2.NO, R3.Pin_1, J1.pin3
  N8: Teensy_LC.Vin, KY-2.ground, C7.1, C8.+, J3.pin1
  N9: D2F1.COM, D2F2.COM, D2F3.COM, D2F4.COM, J1.pin5
  N10: KY-2.NO, LED3.A

notes:
  12V
  USB 5V

custom parts:
  D2F-FL Omron Snap Action Limit Switch with Level: Snap action switch with stainless steel lever.
  Keyes Relay: The Keyes 5V relay module is suitable for SCM development, home appliance control. It uses a 5V~12V TIL control signal which can control DC / AC signal.
