# Fritzing sketch G13 - Uova (saved by Fritzing 0.9.3b)
stripboards: 5

parts:
  Teensy_3_2 = Teensy 3.1  # not connected
  Componente3 = Adafruit MPR121
  J37 = Screw terminal - 2 pins [package=THT]
  J38 = Screw terminal - 2 pins [package=THT]
  R62 = Resistor [tolerance=±5% resistance=1k package=THT]
  D7 = Rectifier Diode [part_number=1N4001 package="300 mil [THT]"]
  Q8 = Basic FET N-Channel [package="TO220 [THT]"]
  J41 = screw terminal, 3 pins
  U5 = Luxeon LED [package=luxeon]
  J36 = screw terminal, 8 pins
  J36_2 = screw terminal, 8 pins
  J44 = screw terminal, 5 pins
  J45 = screw terminal, 3 pins
  J46 = Screw terminal - 2 pins [package=THT]
  J47 = screw terminal, 8 pins
  J48 = screw terminal, 8 pins
  R63 = Resistor [tolerance=±5% resistance=1k package=THT]
  D8 = Rectifier Diode [part_number=1N4001 package="300 mil [THT]"]
  J51 = Screw terminal - 2 pins [package=THT]
  J52 = Screw terminal - 2 pins [package=THT]
  Q9 = Basic FET N-Channel [package="TO220 [THT]"]
  J53 = screw terminal, 3 pins
  U6 = Luxeon LED [package=luxeon]
  R64 = Resistor [tolerance=±5% resistance=1M package="2512 [SMD]"]
  R65 = Resistor [tolerance=±5% resistance=1M package="2512 [SMD]"]
  R66 = Resistor [tolerance=±5% resistance=1M package="2512 [SMD]"]
  R67 = Resistor [tolerance=±5% resistance=1M package="2512 [SMD]"]
  R68 = Resistor [tolerance=±5% resistance=1M package="2512 [SMD]"]
  R69 = Resistor [tolerance=±5% resistance=1M package="2512 [SMD]"]
  R70 = Resistor [tolerance=±5% resistance=1M package="2512 [SMD]"]
  R71 = Resistor [tolerance=±5% resistance=1M package="2512 [SMD]"]
  Teensy1 = Teensy 3.6 (Basic)
  R72 = Resistor [tolerance=±5% resistance=1M package="2512 [SMD]"]
  R73 = Resistor [tolerance=±5% resistance=1M package="2512 [SMD]"]
  R74 = Resistor [tolerance=±5% resistance=1M package="2512 [SMD]"]
  R75 = Resistor [tolerance=±5% resistance=1M package="2512 [SMD]"]
  JP27 = Header 12 [package=1x12_machine-pin-header_lock.004]
  JP33 = Header 12 [package=1x12_machine-pin-header_lock.004]
  J54 = Camdenboss CTB0158-12 [part_number=CTB0158-12 package=THT]
  J43 = screw terminal, 8 pins
  J42 = screw terminal, 5 pins

nets:
  N1: Componente3.GND, J36.pin1, J36_2.pin1
  N2: Componente3.VIN, J38.pin2
  N3: Componente3.SDA, J37.pin1
  N4: Componente3.SCL, J37.pin2, J36.pin8
  N5: R62.Pin_0, Q8.gate
  N6: R62.Pin_1, J41.pin3, J36.pin2, J36_2.pin2
  N7: D7.cathode, Q8.drain, J41.pin1, U5.C
  N8: D7.anode, Q8.source, J41.pin2
  N9: J36.pin3, J36_2.pin3
  N10: J36.pin4, J36_2.pin4
  N11: J36.pin5, J36_2.pin5
  N12: J36.pin6, J36_2.pin6
  N13: J36.pin7, J36_2.pin7
  N14: J44.pin1, Teensy1.A3/D17
  N15: J44.pin2, Teensy1.A4/D18
  N16: J44.pin3, Teensy1.A5/D19
  N17: J44.pin4, Teensy1.A6/D20
  N18: J44.pin5, R63.Pin_1, J53.pin3, Teensy1.A7/D21
  N19: J45.pin1, Teensy1.D33
  N20: J45.pin2, Teensy1.D34
  N21: J45.pin3, Teensy1.D35
  N22: J46.pin1, Teensy1.AGND
  N23: J46.pin2, J48.pin1, J48.pin2, J48.pin3, J48.pin4, J48.pin5, J48.pin6, J48.pin7, J48.pin8, U6.A
  GND: J47.pin1, J47.pin2, J47.pin3, J47.pin4, J47.pin5, J47.pin6, J47.pin7, J47.pin8, D8.anode, Q9.source, J53.pin2, Teensy1.GND, Teensy1.GND1
  N24: R63.Pin_0, Q9.gate
  N25: D8.cathode, Q9.drain, J53.pin1, U6.C
  N26: J51.pin1, Teensy1.D24
  N27: J51.pin2, Teensy1.D25
  N28: J52.pin1, J52.pin2, R64.Pin_0, R65.Pin_0, R66.Pin_0, R67.Pin_0, R68.Pin_0, R69.Pin_0, R70.Pin_0, R71.Pin_0, Teensy1.D1, R72.Pin_0, R73.Pin_0, R74.Pin_0, R75.Pin_0, J43.pin1
  N29: R64.Pin_1, Teensy1.D3, JP27.10, J54.pin11, J43.pin3
  N30: R65.Pin_1, Teensy1.D2, JP27.12, J54.pin12, J43.pin2
  N31: R66.Pin_1, Teensy1.D5, JP27.6, J54.pin9, J43.pin5
  N32: R67.Pin_1, Teensy1.D4, JP27.8, J54.pin10, J43.pin4
  N33: R68.Pin_1, Teensy1.D7, JP27.2, J54.pin7, J43.pin7
  N34: R69.Pin_1, Teensy1.D6, JP27.4, J54.pin8, J43.pin6
  N35: R70.Pin_1, Teensy1.D28, JP33.10, J54.pin5, J42.pin1
  N36: R71.Pin_1, Teensy1.D8, JP33.12, J54.pin6, J43.pin8
  N37: Teensy1.3V3, Teensy1.3V3_1
  N38: Teensy1.D29, R72.Pin_1, JP33.8, J54.pin4, J42.pin2
  N39: Teensy1.D30, R73.Pin_1, JP33.6, J54.pin3, J42.pin3
  N40: Teensy1.D31, R74.Pin_1, JP33.4, J54.pin2, J42.pin4
  N41: Teensy1.D32, R75.Pin_1, JP33.2, J54.pin1, J42.pin5

notes:
  5V 5A
  x6
  Stagnola
  OPPURE

custom parts:
  Adafruit MPR121: Add lots of touch sensors to your next microcontroller project with this easy-to-use 12-channel capacitive touch sensor breakout board, starring the MPR121. This chip can handle up to 12 individual touch pads. The MPR121 has support for only I2C, which can be implemented with nearly any microcontroller. You can select one of 4 addresses with the ADDR pin, for a total of 48 capacitive touch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
  Teensy 3.6 (Basic): The Teensy is a complete USB-based microcontoller development system, in a very small footprint, capable of implementing many types of projects. All programming is done via the USB port. No special programmer is needed, only a standard micro-USB cable and a PC or Macintosh with a USB port.
