# Fritzing sketch G14 - Uccelli (saved by Fritzing 0.9.3b)
stripboards: 3

parts:
  Teensy1 = Teensy 3.6 (Basic)
  J23 = Screw terminal - 2 pins [package=THT]
  J25 = screw terminal, 5 pins
  J26 = screw terminal, 5 pins
  J30 = Screw terminal - 2 pins [package=THT]
  JP17 = Header 1 [package=1x01_offset]
  JP18 = Header 1 [package=1x01_offset]
  JP19 = Header 1 [package=1x01_offset]
  JP20 = Header 1 [package=1x01_offset]
  JP21 = Header 1 [package=1x01_offset]
  JP22 = Header 1 [package=1x01_offset]
  JP23 = Header 1 [package=1x01_offset]
  JP24 = Header 1 [package=1x01_offset]
  R49 = Resistor [tolerance=±5% resistance=1M package="2512 [SMD]"]
  R50 = Resistor [tolerance=±5% resistance=1M package="2512 [SMD]"]
  R51 = Resistor [tolerance=±5% resistance=1M package="2512 [SMD]"]
  R52 = Resistor [tolerance=±5% resistance=1M package="2512 [SMD]"]
  R53 = Resistor [tolerance=±5% resistance=1M package="2512 [SMD]"]
  R54 = Resistor [tolerance=±5% resistance=1M package="2512 [SMD]"]
  R55 = Resistor [tolerance=±5% resistance=1M package="2512 [SMD]"]
  R56 = Resistor [tolerance=±5% resistance=1M package="2512 [SMD]"]
  J28 = screw terminal, 10 pins
  J31 = Screw terminal - 2 pins [package=THT]
  R59 = Resistor [tolerance=±5% resistance=1k package=THT]
  D4 = Rectifier Diode [part_number=1N4001 package="300 mil [THT]"]
  Q5 = Basic FET N-Channel [package="TO220 [THT]"]
  J32 = screw terminal, 3 pins
  U2 = Luxeon LED [package=luxeon]
  J21 = screw terminal, 8 pins
  J22 = screw terminal, 8 pins
  J29 = screw terminal, 6 pins
  J27 = screw terminal, 3 pins
  J24 = screw terminal, 3 pins
  Componente2 = Adafruit MPR121  # not connected

nets:
  GND: Teensy1.GND, Teensy1.GND1, D4.anode, Q5.source, J32.pin2, J22.pin1, J22.pin2, J22.pin3, J22.pin4, J22.pin5, J22.pin6, J22.pin7, J22.pin8
  N1: Teensy1.D4, J26.pin1, JP19.1, R50.Pin_1, J28.pin10
  N2: Teensy1.D5, J26.pin2, JP17.1, R49.Pin_1, J28.pin8
  N3: Teensy1.D6, J26.pin3, JP18.1, R52.Pin_1, J28.pin6
  N4: Teensy1.D7, J26.pin4, JP20.1, R51.Pin_1, J28.pin4
  N5: Teensy1.D8, J26.pin5, JP21.1, R54.Pin_1, J28.pin2
  N6: Teensy1.A3/D17, J25.pin1
  N7: Teensy1.A4/D18, J25.pin2
  N8: Teensy1.A5/D19, J25.pin3
  N9: Teensy1.A6/D20, J25.pin4
  N10: Teensy1.A7/D21, J25.pin5, R59.Pin_1, J32.pin3
  N11: Teensy1.3V3, Teensy1.3V3_1
  N12: Teensy1.AGND, J23.pin1
  N13: Teensy1.D24, J30.pin1, J30.pin2, R49.Pin_0, R50.Pin_0, R51.Pin_0, R52.Pin_0, R53.Pin_0, R54.Pin_0, R55.Pin_0, R56.Pin_0, J31.pin1
  N14: Teensy1.D25, J31.pin2
  N15: Teensy1.D28, JP22.1, R53.Pin_1, J29.pin6, J27.pin1
  N16: Teensy1.D29, JP23.1, R56.Pin_1, J29.pin4, J27.pin2
  N17: Teensy1.D30, JP24.1, R55.Pin_1, J29.pin2, J27.pin3
  N18: Teensy1.D33, J24.pin1
  N19: Teensy1.D34, J24.pin2
  N20: Teensy1.D35, J24.pin3
  N21: J23.pin2, U2.A, J21.pin1, J21.pin2, J21.pin3, J21.pin4, J21.pin5, J21.pin6, J21.pin7, J21.pin8
  N22: R59.Pin_0, Q5.gate
  N23: D4.cathode, Q5.drain, J32.pin1, U2.C

notes:
  Stagnola
  x8
  5V 5A

custom parts:
  Teensy 3.6 (Basic): The Teensy is a complete USB-based microcontoller development system, in a very small footprint, capable of implementing many types of projects. All programming is done via the USB port. No special programmer is needed, only a standard micro-USB cable and a PC or Macintosh with a USB port.
  Adafruit MPR121: Add lots of touch sensors to your next microcontroller project with this easy-to-use 12-channel capacitive touch sensor breakout board, starring the MPR121. This chip can handle up to 12 individual touch pads. The MPR121 has support for only I2C, which can be implemented with nearly any microcontroller. You can select one of 4 addresses with the ADDR pin, for a total of 48 capacitive touch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
