# Fritzing sketch G17 - ManiglieBis (saved by Fritzing 0.9.3b)
stripboards: 1

parts:
  KY-1 = Keyes Relay [package=THT]
  R2 = Resistor [tolerance=±5% resistance=10k package=THT]
  Teensy_3_1 = Teensy 3.1  # not connected
  D2F1 = D2F-FL Omron Snap Action Limit Switch with Level
  KY-2 = Keyes Relay [package=THT]
  D2F2 = D2F-FL Omron Snap Action Limit Switch with Level
  D2F3 = D2F-FL Omron Snap Action Limit Switch with Level
  D2F4 = D2F-FL Omron Snap Action Limit Switch with Level
  R3 = Resistor [tolerance=±5% resistance=10k package=THT]
  R4 = Resistor [tolerance=±5% resistance=10k package=THT]
  R5 = Resistor [tolerance=±5% resistance=10k package=THT]
  J1 = screw terminal, 4 pins
  J3 = Screw terminal - 2 pins [package=THT]
  J4 = screw terminal, 3 pins
  J2 = Screw terminal - 2 pins [package=THT]
  LED3 = LEDs [package=led10mm]
  LED2 = LEDs [package=led10mm]

nets:
  N1: KY-1.signal, J2.pin1
  N2: KY-1.power, D2F1.COM, KY-2.power, D2F2.COM, D2F3.COM, D2F4.COM, J4.pin1, J4.pin2, J4.pin3
  N3: KY-1.ground, KY-2.ground, J3.pin1, J3.pin2
  N4: KY-1.C, KY-2.C, LED2.C
  N5: KY-1.NO, LED2.A
  N6: R2.Pin_0, R3.Pin_0, R4.Pin_0, R5.Pin_0
  N7: R2.Pin_1, D2F1.NO, J1.pin4
  N8: KY-2.signal, J2.pin2
  N9: KY-2.NO, LED3.A
  N10: D2F2.NO, R3.Pin_1, J1.pin3
  N11: D2F3.NO, R4.Pin_1, J1.pin2
  N12: D2F4.NO, R5.Pin_1, J1.pin1

notes:
  220V
  USB 5V

custom parts:
  Keyes Relay: The Keyes 5V relay module is suitable for SCM development, home appliance control. It uses a 5V~12V TIL control signal which can control DC / AC signal.
  D2F-FL Omron Snap Action Limit Switch with Level: Snap action switch with stainless steel lever.
