# Fritzing sketch G18 - Forno (saved by Fritzing 0.9.3b)
stripboards: 1

parts:
  S1 = Reed switch [package=THT]
  KY-1 = Keyes Relay [package=THT]
  J2 = Screw terminal - 2 pins [package=THT]
  J3 = Screw terminal - 2 pins [package=THT]
  R2 = Resistor [tolerance=±5% resistance=10k package=THT]
  M1 = DC Motor
  Teensy_3_1 = Teensy 3.1  # not connected
  R3 = Resistor [tolerance=±5% resistance=10k package=THT]
  J5 = Screw terminal - 2 pins [package=THT]
  S2 = Reed switch [package=THT]
  U1 = POT_SWITCH [package=pot_pth_switch]
  U2 = POT_SWITCH [package=pot_pth_switch]
  KY-2 = Keyes Relay [package=THT]
  J1 = screw terminal, 3 pins
  J4 = screw terminal, 3 pins
  J6 = screw terminal, 4 pins

nets:
  N1: S1.pin_1, J5.pin1, J5.pin2, S2.pin_1, U1.G$2_2, U2.G$2_2, J6.pin4
  N2: S1.pin_2, J3.pin2, R2.Pin_1
  N3: KY-1.signal, J2.pin1
  N4: KY-1.power, M1.pin_2, KY-2.power, J1.pin1, J1.pin2, J1.pin3
  N5: KY-1.ground, KY-1.C, KY-2.ground, J4.pin1, J4.pin2, J4.pin3
  N6: KY-1.NO, M1.pin_1
  N7: J2.pin2, KY-2.signal
  N8: J3.pin1, R3.Pin_1, S2.pin_2
  N9: R2.Pin_0, R3.Pin_0, U1.G$1_A, U2.G$1_A, J6.pin1
  N10: U1.G$2_1, J6.pin2
  N11: U2.G$2_1, J6.pin3

notes:
  USB 5V
  12V
  elettrocalamita + diodo + snubber

custom parts:
  Keyes Relay: The Keyes 5V relay module is suitable for SCM development, home appliance control. It uses a 5V~12V TIL control signal which can control DC / AC signal.
