# Fritzing sketch G19 - Ingranaggi (saved by Fritzing 0.9.3b)
stripboards: 1

parts:
  Teensy_3_3 = Teensy 3.1  # not connected
  D2F7 = D2F-FL Omron Snap Action Limit Switch with Level
  J9 = Screw terminal - 2 pins [package=THT]
  J10 = Screw terminal - 2 pins [package=THT]
  J11 = screw terminal, 3 pins
  J12 = Screw terminal - 2 pins [package=THT]
  R8 = Resistor [tolerance=±5% resistance=10k package=THT]
  KY-2 = Keyes Relay [package=THT]
  M1 = DC Motor

nets:
  N1: D2F7.COM, J11.pin1, J11.pin2, J11.pin3, KY-2.ground, KY-2.C
  N2: D2F7.NO, J9.pin2, R8.Pin_1
  N3: J10.pin1, KY-2.signal
  N4: J12.pin1, J12.pin2, KY-2.power, M1.pin_2
  N5: KY-2.NO, M1.pin_1

notes:
  USB 5V

custom parts:
  D2F-FL Omron Snap Action Limit Switch with Level: Snap action switch with stainless steel lever.
  Keyes Relay: The Keyes 5V relay module is suitable for SCM development, home appliance control. It uses a 5V~12V TIL control signal which can control DC / AC signal.
