# Fritzing sketch G2 - Tastiera (saved by Fritzing 0.9.3b)
stripboards: 2

parts:
  R2 = Resistor [tolerance=±5% resistance=4.7k package=THT]
  Teensy_LC = Teensy 3.1
  D2F1 = D2F-FL Omron Snap Action Limit Switch with Level
  D2F2 = D2F-FL Omron Snap Action Limit Switch with Level
  D2F3 = D2F-FL Omron Snap Action Limit Switch with Level
  D2F4 = D2F-FL Omron Snap Action Limit Switch with Level
  R3 = Resistor [tolerance=±5% resistance=4.7k package=THT]
  C7 = Ceramic Capacitor [capacitance=100nF package="100 mil [THT, multilayer]"]
  C8 = Electrolytic Capacitor [capacitance=1µF package="100 mil [THT, electrolytic]"]
  J1 = Screw terminal - 2 pins [package=THT]
  J2 = Screw terminal - 2 pins [package=THT]
  J3 = Screw terminal - 2 pins [package=THT]
  J4 = Camdenboss CTB0158-2 [part_number=CTB0158-2 package=THT]
  J5 = Camdenboss CTB0158-2 [part_number=CTB0158-2 package=THT]
  J6 = Camdenboss CTB0158-2 [part_number=CTB0158-2 package=THT]
  J7 = Camdenboss CTB0158-2 [part_number=CTB0158-2 package=THT]
  JP1 = Header 8 [package=1x08_smd_alt]
  J8 = Camdenboss CTB0158-2 [part_number=CTB0158-2 package=THT]
  R4 = Resistor [tolerance=±5% resistance=10k package=THT]
  R5 = Resistor [tolerance=±5% resistance=10k package=THT]
  R6 = Resistor [tolerance=±5% resistance=10k package=THT]
  R7 = Resistor [tolerance=±5% resistance=10k package=THT]
  R9 = Resistor [tolerance=±5% resistance=10k package=THT]
  R10 = Resistor [tolerance=±5% resistance=10k package=THT]
  R11 = Resistor [tolerance=±5% resistance=10k package=THT]
  R12 = Resistor [tolerance=±5% resistance=10k package=THT]
  J9 = Camdenboss CTB0158-2 [part_number=CTB0158-2 package=THT]

nets:
  N1: R2.Pin_0, Teensy_LC.3V3, R3.Pin_0
  N2: R2.Pin_1, Teensy_LC.A5/D19, J2.pin2
  N3: Teensy_LC.GND, D2F1.COM, D2F2.COM, D2F3.COM, D2F4.COM, C7.0, C8.-, J3.pin2
  N4: Teensy_LC.A4/D18, R3.Pin_1, J2.pin1
  N5: Teensy_LC.Vin, C7.1, C8.+, J1.pin2
  N6: D2F1.NO, JP1.1, R4.Pin_0
  N7: D2F4.NO, J6.pin2, JP1.8
  N8: J1.pin1, J7.pin2, J8.pin1, R4.Pin_1, R5.Pin_1, R6.Pin_1, R7.Pin_1, R9.Pin_1, R10.Pin_1, R11.Pin_1, R12.Pin_0, J9.pin1
  N9: J4.pin1, JP1.3, R6.Pin_0
  N10: J4.pin2, JP1.4, R7.Pin_0
  N11: J5.pin1, JP1.5, R5.Pin_0
  N12: J5.pin2, JP1.6, R10.Pin_0
  N13: J6.pin1, JP1.7, R11.Pin_0
  N14: JP1.2, R9.Pin_0
  N15: J8.pin2, J9.pin2

notes:
  PCF8574
  (x4)
  USB 5V
  x 24
  5V 5A

custom parts:
  D2F-FL Omron Snap Action Limit Switch with Level: Snap action switch with stainless steel lever.
