# Fritzing sketch G3 - Liane (saved by Fritzing 0.9.3b)
stripboards: 1

parts:
  Componente3 = RFID-RC522-v2
  Teensy_3_4 = Teensy 3.1
  Componente4 = RFID-RC522-v2
  Componente5 = RFID-RC522-v2
  J19 = screw terminal, 3 pins
  J25 = screw terminal, 3 pins
  J11 = screw terminal, 3 pins
  J26 = screw terminal, 3 pins
  J12 = screw terminal, 3 pins
  J13 = screw terminal, 6 pins

nets:
  N1: Componente3.SDA, Teensy_3_4.A1/D15, J13.pin2
  N2: Componente3.SCK, Teensy_3_4.D13, Componente4.SCK, Componente5.SCK, J12.pin1, J12.pin2, J12.pin3
  N3: Componente3.MOSI, Teensy_3_4.D11, Componente4.MOSI, Componente5.MOSI, J26.pin1, J26.pin2, J26.pin3
  N4: Componente3.MISO, Teensy_3_4.D12, Componente4.MISO, Componente5.MISO, J11.pin1, J11.pin2, J11.pin3
  GND: Componente3.GND, Teensy_3_4.GND, Componente4.GND, Componente5.GND, J25.pin1, J25.pin2, J25.pin3
  N5: Componente3.RST, Componente4.RST, Componente5.RST, J13.pin4, J13.pin5, J13.pin6
  3.3V: Componente3.3.3V, Teensy_3_4.3V3, Componente4.3.3V, Componente5.3.3V, J19.pin1, J19.pin2, J19.pin3
  N6: Teensy_3_4.A0/D14, Componente4.SDA, J13.pin1
  N7: Teensy_3_4.A2/D16, Componente5.SDA, J13.pin3

notes:
  5V USB
  cavi schermati twistati (di rete) non più lontani di 10'
  se problemi diminuire la frequenza del clock dell'SPI

custom parts:
  RFID-RC522-v2: A simple China made RFID-RC522 Reader; do check the pin labels, as this is a MFRC522 based clone.
