# Fritzing sketch G3 - Testa totem (saved by Fritzing 0.9.3b)
stripboards: 1

parts:
  Teensy_3_1 = Teensy 3.1  # not connected
  C7 = Ceramic Capacitor [capacitance=100nF package="100 mil [THT, multilayer]"]
  C8 = Electrolytic Capacitor [capacitance=0.22mF package="100 mil [THT, electrolytic]"]
  J30 = screw terminal, 8 pins
  Componente7 = RFID-RC522-v2

nets:
  N1: C7.0, C8.+
  N2: C7.1, C8.-
  N3: J30.pin1, Componente7.3.3V
  N4: J30.pin2, Componente7.RST
  N5: J30.pin3, Componente7.GND
  N6: J30.pin5, Componente7.MISO
  N7: J30.pin6, Componente7.MOSI
  N8: J30.pin7, Componente7.SCK
  N9: J30.pin8, Componente7.SDA

notes:
  USB 5V
  Load Cell

custom parts:
  RFID-RC522-v2: A simple China made RFID-RC522 Reader; do check the pin labels, as this is a MFRC522 based clone.
