# Fritzing sketch G4 - Liane (saved by Fritzing 0.9.3b)
stripboards: 1

parts:
  Componente3 = RFID-RC522-v2
  Componente4 = RFID-RC522-v2
  Componente5 = RFID-RC522-v2
  Teensy_3_5 = Teensy 3.1
  J28 = screw terminal, 8 pins
  J29 = screw terminal, 8 pins
  J30 = screw terminal, 8 pins
  J31 = screw terminal, 3 pins
  R1 = Resistor [tolerance=±5% resistance=10k package=THT]
  R2 = Resistor [tolerance=±5% resistance=10k package=THT]
  R3 = Resistor [tolerance=±5% resistance=10k package=THT]

nets:
  N1: Componente3.SDA, Teensy_3_5.A1/D15, J28.pin8, R1.Pin_0
  N2: Componente3.SCK, Componente4.SCK, Componente5.SCK, Teensy_3_5.D13, J28.pin7, J29.pin7, J30.pin2
  N3: Componente3.MOSI, Componente4.MOSI, Componente5.MOSI, Teensy_3_5.D11, J28.pin6, J29.pin6, J30.pin3
  N4: Componente3.MISO, Componente4.MISO, Componente5.MISO, J28.pin5, J29.pin5, J30.pin4
  GND: Componente3.GND, Componente4.GND, Componente5.GND, Teensy_3_5.AGND, J28.pin3, J29.pin3, J30.pin6
  N5: Componente3.RST, Componente4.RST, Componente5.RST, Teensy_3_5.A3/D17, J28.pin2, J29.pin2, J30.pin7
  3.3V: Componente3.3.3V, Componente4.3.3V, Componente5.3.3V, Teensy_3_5.3V3, J28.pin1, J29.pin1, J30.pin8, R1.Pin_1, R2.Pin_1, R3.Pin_1
  N6: Componente4.SDA, Teensy_3_5.A0/D14, J30.pin1, R3.Pin_0
  N7: Componente5.SDA, Teensy_3_5.A2/D16, J29.pin8, R2.Pin_0
  N8: Teensy_3_5.Vin, J31.pin2

notes:
  5V USB
  cavi schermati twistati (di rete) non più lontani di 10'
  se problemi diminuire la frequenza del clock dell'SPI

custom parts:
  RFID-RC522-v2: A simple China made RFID-RC522 Reader; do check the pin labels, as this is a MFRC522 based clone.
