# Fritzing sketch G4 - Roccia (saved by Fritzing 0.9.3b)
stripboards: 2

parts:
  KY-2 = Keyes Relay [package=THT]
  KY-3 = Keyes Relay [package=THT]
  R25 = Resistor [tolerance=±5% resistance=1M package="2512 [SMD]"]
  R26 = Resistor [tolerance=±5% resistance=1M package="2512 [SMD]"]
  R30 = Resistor [tolerance=±5% resistance=1M package="2512 [SMD]"]
  R32 = Resistor [tolerance=±5% resistance=1M package="2512 [SMD]"]
  R34 = Resistor [tolerance=±5% resistance=1M package="2512 [SMD]"]
  R36 = Resistor [tolerance=±5% resistance=1M package="2512 [SMD]"]
  R38 = Resistor [tolerance=±5% resistance=1M package="2512 [SMD]"]
  R40 = Resistor [tolerance=±5% resistance=1M package="2512 [SMD]"]
  R42 = Resistor [tolerance=±5% resistance=1M package="2512 [SMD]"]
  R44 = Resistor [tolerance=±5% resistance=1M package="2512 [SMD]"]
  R46 = Resistor [tolerance=±5% resistance=1M package="2512 [SMD]"]
  R48 = Resistor [tolerance=±5% resistance=1M package="2512 [SMD]"]
  J1 = Screw terminal - 2 pins [package=THT]
  J2 = screw terminal, 12 pins
  J3 = screw terminal, 12 pins
  JP1 = Header 1 [package=1x01_offset]
  JP2 = Header 1 [package=1x01_offset]
  JP3 = Header 1 [package=1x01_offset]
  JP4 = Header 1 [package=1x01_offset]
  JP5 = Header 1 [package=1x01_offset]
  JP6 = Header 1 [package=1x01_offset]
  JP7 = Header 1 [package=1x01_offset]
  JP8 = Header 1 [package=1x01_offset]
  JP9 = Header 1 [package=1x01_offset]
  JP10 = Header 1 [package=1x01_offset]
  JP11 = Header 1 [package=1x01_offset]
  JP12 = Header 1 [package=1x01_offset]
  R49 = Resistor [tolerance=±5% resistance=1M package="2512 [SMD]"]
  R50 = Resistor [tolerance=±5% resistance=1M package="2512 [SMD]"]
  R51 = Resistor [tolerance=±5% resistance=1M package="2512 [SMD]"]
  R52 = Resistor [tolerance=±5% resistance=1M package="2512 [SMD]"]
  R53 = Resistor [tolerance=±5% resistance=1M package="2512 [SMD]"]
  R54 = Resistor [tolerance=±5% resistance=1M package="2512 [SMD]"]
  R55 = Resistor [tolerance=±5% resistance=1M package="2512 [SMD]"]
  R56 = Resistor [tolerance=±5% resistance=1M package="2512 [SMD]"]
  R57 = Resistor [tolerance=±5% resistance=1M package="2512 [SMD]"]
  R58 = Resistor [tolerance=±5% resistance=1M package="2512 [SMD]"]
  R59 = Resistor [tolerance=±5% resistance=1M package="2512 [SMD]"]
  R60 = Resistor [tolerance=±5% resistance=1M package="2512 [SMD]"]
  J4 = Screw terminal - 2 pins [package=THT]
  J5 = screw terminal, 12 pins
  J6 = screw terminal, 12 pins
  JP13 = Header 1 [package=1x01_offset]
  JP14 = Header 1 [package=1x01_offset]
  JP15 = Header 1 [package=1x01_offset]
  JP16 = Header 1 [package=1x01_offset]
  JP17 = Header 1 [package=1x01_offset]
  JP18 = Header 1 [package=1x01_offset]
  JP19 = Header 1 [package=1x01_offset]
  JP20 = Header 1 [package=1x01_offset]
  JP21 = Header 1 [package=1x01_offset]
  JP22 = Header 1 [package=1x01_offset]
  JP23 = Header 1 [package=1x01_offset]
  JP24 = Header 1 [package=1x01_offset]
  Componente2 = Arduino Mega 2560 (Rev3)

nets:
  N1: KY-2.signal, Componente2.D16_PWM/TX2
  N2: KY-2.power, KY-3.power, Componente2.5V
  N3: KY-2.ground, KY-3.ground, Componente2.GND
  N4: KY-3.signal, Componente2.D17_PWM/RX2
  N5: R25.Pin_0, R26.Pin_0, R30.Pin_0, R32.Pin_0, R34.Pin_0, R36.Pin_0, R38.Pin_0, R40.Pin_0, R42.Pin_0, R44.Pin_0, R46.Pin_0, R48.Pin_0, J1.pin1, J1.pin2, R49.Pin_0, R50.Pin_0, R51.Pin_0, R52.Pin_0, R53.Pin_0, R54.Pin_0, R55.Pin_0, R56.Pin_0, R57.Pin_0, R58.Pin_0, R59.Pin_0, R60.Pin_0, J4.pin1, J4.pin2, Componente2.D24
  N6: R25.Pin_1, J2.pin2, JP9.1, Componente2.D49
  N7: R26.Pin_1, J2.pin4, JP11.1, Componente2.D48
  N8: R30.Pin_1, J2.pin8, JP10.1, Componente2.D46
  N9: R32.Pin_1, J2.pin6, JP12.1, Componente2.D47
  N10: R34.Pin_1, J2.pin12, JP2.1, Componente2.D44
  N11: R36.Pin_1, J2.pin10, JP1.1, Componente2.D45
  N12: R38.Pin_1, J3.pin4, JP4.1, Componente2.D42
  N13: R40.Pin_1, J3.pin2, JP3.1, Componente2.D43
  N14: R42.Pin_1, J3.pin8, JP7.1, Componente2.D40
  N15: R44.Pin_1, J3.pin6, JP5.1, Componente2.D41
  N16: R46.Pin_1, J3.pin12, JP6.1, Componente2.D38
  N17: R48.Pin_1, J3.pin10, JP8.1, Componente2.D39
  N18: R49.Pin_1, J5.pin10, JP17.1, Componente2.D27
  N19: R50.Pin_1, J5.pin12, JP21.1, Componente2.D26
  N20: R51.Pin_1, J5.pin6, JP16.1, Componente2.D29
  N21: R52.Pin_1, J5.pin8, JP19.1, Componente2.D28
  N22: R53.Pin_1, J5.pin2, JP20.1, Componente2.D31
  N23: R54.Pin_1, J5.pin4, JP24.1, Componente2.D30
  N24: R55.Pin_1, J6.pin10, JP13.1, Componente2.D33
  N25: R56.Pin_1, J6.pin12, JP22.1, Componente2.D32
  N26: R57.Pin_1, J6.pin6, JP15.1, Componente2.D35
  N27: R58.Pin_1, J6.pin8, JP18.1, Componente2.D34
  N28: R59.Pin_1, J6.pin4, JP23.1, Componente2.D36
  N29: R60.Pin_1, J6.pin2, JP14.1, Componente2.D37

notes:
  Stagnola
  12V
  elettrocalamita
  quadro
  elettrocalamita
  Botola
  USB 5V

custom parts:
  Keyes Relay: The Keyes 5V relay module is suitable for SCM development, home appliance control. It uses a 5V~12V TIL control signal which can control DC / AC signal.
