# Fritzing sketch G5 - Roccia (saved by Fritzing 0.9.3b)
stripboards: 1

parts:
  Teensy_3_1 = Teensy 3.1
  D2F4 = D2F-FL Omron Snap Action Limit Switch with Level
  R5 = Resistor [tolerance=±5% resistance=10k package=THT]
  J3 = Screw terminal - 2 pins [package=THT]  # not connected
  KY-1 = Keyes Relay [package=THT]
  J1 = screw terminal, 3 pins

nets:
  N1: Teensy_3_1.A6/D20, D2F4.NO, R5.Pin_1
  N2: Teensy_3_1.A7/D21, KY-1.signal
  N3: Teensy_3_1.3V3, R5.Pin_0
  N4: Teensy_3_1.AGND, D2F4.COM, KY-1.ground, J1.pin1
  N5: Teensy_3_1.Vin, KY-1.power, J1.pin2

notes:
  12V
  USB 5V

custom parts:
  D2F-FL Omron Snap Action Limit Switch with Level: Snap action switch with stainless steel lever.
  Keyes Relay: The Keyes 5V relay module is suitable for SCM development, home appliance control. It uses a 5V~12V TIL control signal which can control DC / AC signal.
