# Fritzing sketch G5 - Tamburo (saved by Fritzing 0.9.3b)
stripboards: 1

parts:
  Teensy_3_2 = Teensy 3.1  # not connected
  R6 = Resistor [tolerance=±5% resistance=1M package=THT]
  J9 = Piezo Speaker
  J11 = Screw terminal - 2 pins [package=THT]
  U1 = DIODE-ZENER [package=diode-zener]
  R7 = Resistor [tolerance=±5% resistance=470 package=THT]

nets:
  N1: R6.Pin_0, J9.pin1, J11.pin2, U1.A
  N2: R6.Pin_1, J9.pin2, J11.pin1, U1.C, R7.Pin_0

notes:
  USB 5V
  Trigger di schmitt
  74HC14 per rilevare il segnale ( più resistenza e condensatore prima)
  altrimenti amplificare il segnale
