# Fritzing sketch G6 - Tamburo (saved by Fritzing 0.9.3b)
stripboards: 2

parts:
  Teensy_3_2 = Teensy 3.1  # not connected
  R6 = Resistor [tolerance=±5% resistance=1M package=THT]
  J9 = Piezo Speaker  # not connected
  U1 = DIODE-ZENER [package=diode-zener]
  R7 = Resistor [tolerance=±5% resistance=470 package=THT]
  J11 = screw terminal, 3 pins
  J12 = Screw terminal - 2 pins [package=THT]
  J13 = Screw terminal - 2 pins [package=THT]

nets:
  N1: R6.Pin_1, U1.C, R7.Pin_0, J12.pin1
  N2: R7.Pin_1, J13.pin2
  N3: J11.pin2, J12.pin2, J13.pin1

notes:
  USB 5V
  Trigger di schmitt
  74HC14 per rilevare il segnale ( più resistenza e condensatore prima)
  altrimenti amplificare il segnale
