# Fritzing sketch G6 - Totem (saved by Fritzing 0.9.3b)
stripboards: 1

parts:
  Teensy_3_2 = Teensy 3.1  # not connected
  HC-SR04_Sensor_1 = HC-SR04 Ultrasonic Distance Sensor
  HC-SR04_Sensor_2 = HC-SR04 Ultrasonic Distance Sensor
  J11 = screw terminal, 8 pins
  J12 = screw terminal, 4 pins
  KY-1 = Keyes Relay [package=THT]
  KY-2 = Keyes Relay [package=THT]
  KY-3 = Keyes Relay [package=THT]
  J13 = screw terminal, 4 pins

nets:
  VCC: HC-SR04_Sensor_1.VCC, HC-SR04_Sensor_2.VCC, J11.pin8, J12.pin1, J12.pin2, J12.pin3, J12.pin4, KY-1.power, KY-2.power, KY-3.power
  N1: HC-SR04_Sensor_1.TRIG, J11.pin4
  N2: HC-SR04_Sensor_1.ECHO, J11.pin5
  GND: HC-SR04_Sensor_1.GND, HC-SR04_Sensor_2.GND, J11.pin7
  N3: HC-SR04_Sensor_2.TRIG, J11.pin2
  N4: HC-SR04_Sensor_2.ECHO, J11.pin3
  N5: KY-1.signal, J13.pin2
  N6: KY-1.ground, KY-2.ground, KY-3.ground, J13.pin1
  N7: KY-2.signal, J13.pin3
  N8: KY-3.signal, J13.pin4

notes:
  USB 5V
  sequenza luci + elettrovalvola
  luce alta
  luce bassa
  elet valv

custom parts:
  Keyes Relay: The Keyes 5V relay module is suitable for SCM development, home appliance control. It uses a 5V~12V TIL control signal which can control DC / AC signal.
