# Fritzing sketch G7 - Totem (saved by Fritzing 0.9.3b)
stripboards: 1

parts:
  Teensy_3_2 = Teensy 3.1  # not connected
  U3 = HC-SR04 [chip_label=IC package="SIP (Single Inline) [THT]"]
  U4 = HC-SR04 [chip_label=IC package="SIP (Single Inline) [THT]"]
  J11 = screw terminal, 5 pins
  J15 = screw terminal, 5 pins
  KY-2 = Keyes Relay [package=THT]
  KY-3 = Keyes Relay [package=THT]
  J16 = screw terminal, 3 pins
  J17 = screw terminal, 3 pins

nets:
  N1: U3.Trig, J11.pin4
  N2: U3.Echo, J11.pin5
  N3: U4.Vcc, J11.pin1, J15.pin4, KY-2.power, KY-3.power, J16.pin3, J17.pin2
  N4: U4.Trig, J15.pin3
  N5: U4.Echo, J15.pin2
  N6: U4.GND, J15.pin1, KY-3.ground, J17.pin3
  N7: KY-2.signal, J16.pin1
  N8: KY-2.ground, J16.pin2
  N9: KY-3.signal, J17.pin1

notes:
  USB 5V
  sequenza luci + elettrovalvola

custom parts:
  HC-SR04: HC-SR04 ultrasound distance sensor
  Keyes Relay: The Keyes 5V relay module is suitable for SCM development, home appliance control. It uses a 5V~12V TIL control signal which can control DC / AC signal.
