# Fritzing sketch G9 - Braciere (saved by Fritzing 0.9.3b)
stripboards: 1

parts:
  Teensy_3_2 = Teensy 3.1
  D2F5 = D2F-FL Omron Snap Action Limit Switch with Level
  J7 = screw terminal, 3 pins
  R6 = Resistor [tolerance=±5% resistance=10k package=THT]
  KY-1 = Keyes Relay [package=THT]
  R7 = Resistor [tolerance=±5% resistance=10k package=THT]
  D2F6 = D2F-FL Omron Snap Action Limit Switch with Level
  C9 = Ceramic Capacitor [capacitance=100nF package="100 mil [THT, multilayer]"]
  C10 = Electrolytic Capacitor [capacitance=1µF package="100 mil [THT, electrolytic]"]
  J31 = screw terminal, 8 pins
  Componente8 = RFID-RC522-v2
  J5 = screw terminal, 3 pins

nets:
  N1: Teensy_3_2.GND, J7.pin2, KY-1.ground, C9.0, C10.-
  N2: Teensy_3_2.A5/D19, J31.pin4
  3V3: Teensy_3_2.3V3, R6.Pin_0, R7.Pin_0, J31.pin1, Componente8.3.3V
  N3: Teensy_3_2.Vin, J7.pin1, KY-1.power, C9.1, C10.+
  N4: D2F5.COM, D2F6.COM, J31.pin3, Componente8.GND, J5.pin3
  N5: D2F5.NO, R6.Pin_1, R7.Pin_1, D2F6.NO, J31.pin6, Componente8.MOSI, J5.pin1, J5.pin2
  N6: J7.pin3, KY-1.signal
  N7: J31.pin2, Componente8.RST
  N8: J31.pin5, Componente8.MISO
  N9: J31.pin7, Componente8.SCK
  N10: J31.pin8, Componente8.SDA

notes:
  USB 5V
  12V
  elettrocalamita + diodo + snubber

custom parts:
  D2F-FL Omron Snap Action Limit Switch with Level: Snap action switch with stainless steel lever.
  Keyes Relay: The Keyes 5V relay module is suitable for SCM development, home appliance control. It uses a 5V~12V TIL control signal which can control DC / AC signal.
  RFID-RC522-v2: A simple China made RFID-RC522 Reader; do check the pin labels, as this is a MFRC522 based clone.
