# Fritzing sketch G9 - Porta (saved by Fritzing 0.9.3b)
stripboards: 1

parts:
  Teensy_3_3 = Teensy 3.1  # not connected
  R7 = Resistor [tolerance=±5% resistance=1M package=THT]
  J12 = Piezo Speaker
  J13 = Screw terminal - 2 pins [package=THT]
  J14 = Piezo Speaker
  J15 = Piezo Speaker
  J16 = Piezo Speaker
  J17 = screw terminal, 3 pins
  R8 = Resistor [tolerance=±5% resistance=1M package=THT]
  R9 = Resistor [tolerance=±5% resistance=1M package=THT]
  R10 = Resistor [tolerance=±5% resistance=1M package=THT]

nets:
  N1: R7.Pin_0, J12.pin1, J12.pin2, J13.pin2, J14.pin2, J15.pin2, J16.pin1, J16.pin2, J17.pin2, J17.pin3, R8.Pin_0, R8.Pin_1, R9.Pin_0, R9.Pin_1, R10.Pin_0
  N2: R7.Pin_1, J13.pin1, J14.pin1
  N3: J15.pin1, J17.pin1, R10.Pin_1

notes:
  USB 5V
  trigger di schmitt
  74hc14
