# Fritzing sketch G9 - Uova (saved by Fritzing 0.9.3b)
stripboards: 2

parts:
  Teensy_3_2 = Teensy 3.1  # not connected
  Componente3 = Adafruit MPR121
  J37 = Screw terminal - 2 pins [package=THT]
  J38 = Screw terminal - 2 pins [package=THT]
  R62 = Resistor [tolerance=±5% resistance=1k package=THT]
  D7 = Rectifier Diode [part_number=1N4001 package="300 mil [THT]"]
  Q8 = Basic FET N-Channel [package="TO220 [THT]"]
  J41 = screw terminal, 3 pins
  U5 = Luxeon LED [package=luxeon]
  J36 = screw terminal, 8 pins
  J36_2 = screw terminal, 8 pins

nets:
  N1: Componente3.GND, J36.pin1, J36_2.pin1
  N2: Componente3.VIN, J38.pin2
  N3: Componente3.SDA, J37.pin1
  N4: Componente3.SCL, J37.pin2, J36.pin8
  N5: R62.Pin_0, Q8.gate
  N6: R62.Pin_1, J41.pin3, J36.pin2, J36_2.pin2
  N7: D7.cathode, Q8.drain, J41.pin1, U5.C
  N8: D7.anode, Q8.source, J41.pin2
  N9: J36.pin3, J36_2.pin3
  N10: J36.pin4, J36_2.pin4
  N11: J36.pin5, J36_2.pin5
  N12: J36.pin6, J36_2.pin6
  N13: J36.pin7, J36_2.pin7

notes:
  12V 5A
  x6
  Stagnola
  OPPURE
  relay al posto del mosfet

custom parts:
  Adafruit MPR121: Add lots of touch sensors to your next microcontroller project with this easy-to-use 12-channel capacitive touch sensor breakout board, starring the MPR121. This chip can handle up to 12 individual touch pads. The MPR121 has support for only I2C, which can be implemented with nearly any microcontroller. You can select one of 4 addresses with the ADDR pin, for a total of 48 capacitive touch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
